// Logisim project BLI201V32I.circ as structural Verilog: 9 circuits, main circuit main
module main (
);

  wire and_1_out, clk, comparator_1_eq, comparator_2_eq, comparator_3_eq, led0_b, led0_g, led0_r, or_1_out,
       por_1_out, RESET_out, rst;
  wire [3:0] btn, core2dtim_wmask, core2mmio_wmask, ledd, sw;
  wire [31:0] core2dtim_addr, core2dtim_wdata, core2itim_addr, core2mmio_addr, core2mmio_wdata,
       dtim2core_rdata, itim2core_rdata, mmio2core_rdata;
  wire [31:4] register_2_q;

  Clock clock_1 (.out(clk));
  LED led_1 (.in(ledd[3]));
  // RGBLED rgbled_1: pin names not known; wires that end beside it: led0_r, led0_g, led0_b
  RAM #(.addrWidth(24), .asyncread("true"), .dataWidth(32), .databus("bidir")) ITIM (
    .addr(core2itim_addr[25:2]), .we(1'b0), .oe(1'b1), .clk(clk), .data(itim2core_rdata));
  LED led_2 (.in(ledd[2]));
  // RGBLED rgbled_2: pin names not known; wires that end beside it: led0_r, led0_g, led0_b
  LED led_3 (.in(ledd[1]));
  // RGBLED rgbled_3: pin names not known; wires that end beside it: led0_r, led0_g, led0_b
  LED led_4 (.in(ledd[0]));
  // RGBLED rgbled_4: pin names not known; wires that end beside it: led0_r, led0_g, led0_b
  DipSwitch #(.number(4)) dipswitch_1 (.sw1(sw[3]), .sw2(sw[2]), .sw3(sw[1]), .sw4(sw[0]));
  Register #(.width(32)) register_1 (
    .D({{24{1'b0}}, sw, btn}), .en(comparator_1_eq), .clk(clk), .Q(mmio2core_rdata), .clr(rst));
  Comparator #(.width(32)) comparator_1 (.a(core2mmio_addr), .b({32{1'b0}}), .eq(comparator_1_eq));  // open: gt, lt
  Register #(.width(32)) register_2 (
    .D(core2mmio_wdata), .en(comparator_2_eq), .clk(clk), .Q({register_2_q, ledd}), .clr(rst));
  Comparator #(.width(32)) comparator_2 (.a(core2mmio_addr), .b(32'h4), .eq(comparator_2_eq));  // open: gt, lt
  Button button_1 (.out(btn[3]));
  Button button_2 (.out(btn[2]));
  Button button_3 (.out(btn[1]));
  core core_1 (
    .clk(clk), .rst(rst), .core_i_itim_rdata(itim2core_rdata), .core_i_dtim_rdata(dtim2core_rdata),
    .core_i_mmio_rdata(mmio2core_rdata), .core_o_itim_addr(core2itim_addr),
    .core_o_dtim_addr(core2dtim_addr), .core_o_dtim_wmask(core2dtim_wmask),
    .core_o_dtim_wdata(core2dtim_wdata), .core_o_mmio_addr(core2mmio_addr),
    .core_o_mmio_wmask(core2mmio_wmask), .core_o_mmio_wdata(core2mmio_wdata));
  Button button_4 (.out(btn[0]));
  or or_1 (or_1_out, core2dtim_wmask[3], core2dtim_wmask[2], core2dtim_wmask[1], core2dtim_wmask[0]);
  Comparator #(.width(6)) comparator_3 (
    .a(core2dtim_addr[31:26]), .b({6{1'b0}}), .eq(comparator_3_eq));  // open: gt, lt
  and and_1 (and_1_out, comparator_3_eq, or_1_out);
  RAM #(.addrWidth(24), .asyncread("true"), .byteenables("byteEnables"), .dataWidth(32)) DTIM (
    .addr(core2dtim_addr[25:2]), .we(and_1_out), .oe(1'b1), .clk(clk), .din(core2dtim_wdata),
    .dout(dtim2core_rdata), .be3(core2dtim_wmask[3]), .be2(core2dtim_wmask[2]), .be1(core2dtim_wmask[1]),
    .be0(core2dtim_wmask[0]));
  POR por_1 (.out(por_1_out));
  Button #(.press("passive")) RESET (.out(RESET_out));
  and and_2 (rst, ~por_1_out, RESET_out);  // AND_Gate

  // Notes on the sheet:
  //   ARTY A7
endmodule

module core (
  input  clk,
  input  rst,
  input  [31:0] core_i_itim_rdata,
  input  [31:0] core_i_dtim_rdata,
  input  [31:0] core_i_mmio_rdata,
  output [31:0] core_o_itim_addr,
  output [31:0] core_o_dtim_addr,
  output [3:0] core_o_dtim_wmask,
  output [31:0] core_o_dtim_wdata,
  output [31:0] core_o_mmio_addr,
  output [3:0] core_o_mmio_wmask,
  output [31:0] core_o_mmio_wdata
);

  wire biu_1_biu_o_halt, exu_1_exu_o_branch_taken, idu_1_idu_o_is_jump, idu_1_idu_o_is_store;
  wire [1:0] idu_1_idu_o_a_sel, idu_1_idu_o_b_sel;
  wire [2:0] idu_1_idu_o_wb_sel;
  wire [3:0] idu_1_idu_o_br_sel, memu_1_memu_o_dwmask;
  wire [4:0] idu_1_idu_o_fmt_sel;
  wire [10:0] idu_1_idu_o_alu_sel;
  wire [31:0] biu_1_biu_o_drdata, biu_1_biu_o_idata, exu_1_exu_o_exu_data, exu_1_exu_o_rs2_data,
       idu_1_idu_o_imm, idu_1_idu_o_rs1_data, idu_1_idu_o_rs2_data, ifu_1_ifu_o_iaddr, ifu_1_ifu_o_inst,
       ifu_1_ifu_o_pc, memu_1_memu_o_daddr, memu_1_memu_o_data, memu_1_memu_o_dwdata, wbu_1_wbu_o_wb_data;

  ifu ifu_1 (
    .clk(clk), .rst(rst), .ifu_i_halt(biu_1_biu_o_halt), .ifu_i_is_jump(idu_1_idu_o_is_jump),
    .ifu_i_is_branch_taken(exu_1_exu_o_branch_taken), .ifu_i_pc_target(exu_1_exu_o_exu_data),
    .ifu_i_idata(biu_1_biu_o_idata), .ifu_o_pc(ifu_1_ifu_o_pc), .ifu_o_inst(ifu_1_ifu_o_inst),
    .ifu_o_iaddr(ifu_1_ifu_o_iaddr));
  idu idu_1 (
    .clk(clk), .rst(rst), .idu_i_inst(ifu_1_ifu_o_inst), .idu_i_rd_data(wbu_1_wbu_o_wb_data),
    .idu_o_is_jump(idu_1_idu_o_is_jump), .idu_o_rs1_data(idu_1_idu_o_rs1_data),
    .idu_o_rs2_data(idu_1_idu_o_rs2_data), .idu_o_imm(idu_1_idu_o_imm), .idu_o_a_sel(idu_1_idu_o_a_sel),
    .idu_o_b_sel(idu_1_idu_o_b_sel), .idu_o_alu_sel(idu_1_idu_o_alu_sel), .idu_o_br_sel(idu_1_idu_o_br_sel),
    .idu_o_is_store(idu_1_idu_o_is_store), .idu_o_fmt_sel(idu_1_idu_o_fmt_sel),
    .idu_o_wb_sel(idu_1_idu_o_wb_sel));
  biu biu_1 (
    .clk(clk), .rst(rst), .biu_i_iaddr(ifu_1_ifu_o_iaddr), .biu_i_daddr(memu_1_memu_o_daddr),
    .biu_i_dwmask(memu_1_memu_o_dwmask), .biu_i_dwdata(memu_1_memu_o_dwdata),
    .biu_i_itim_rdata(core_i_itim_rdata), .biu_i_dtim_rdata(core_i_dtim_rdata),
    .biu_i_mmio_rdata(core_i_mmio_rdata), .biu_o_halt(biu_1_biu_o_halt), .biu_o_idata(biu_1_biu_o_idata),
    .biu_o_drdata(biu_1_biu_o_drdata), .biu_o_itim_addr(core_o_itim_addr),
    .biu_o_dtim_addr(core_o_dtim_addr), .biu_o_dtim_wmask(core_o_dtim_wmask),
    .biu_o_dtim_wdata(core_o_dtim_wdata), .biu_o_mmio_addr(core_o_mmio_addr),
    .biu_o_mmio_wmask(core_o_mmio_wmask), .biu_o_mmio_wdata(core_o_mmio_wdata));
  exu exu_1 (
    .clk(clk), .rst(rst), .exu_i_pc(ifu_1_ifu_o_pc), .exu_i_rs1_data(idu_1_idu_o_rs1_data),
    .exu_i_rs2_data(idu_1_idu_o_rs2_data), .exu_i_imm(idu_1_idu_o_imm), .exu_i_a_sel(idu_1_idu_o_a_sel),
    .exu_i_b_sel(idu_1_idu_o_b_sel), .exu_i_alu_sel(idu_1_idu_o_alu_sel), .exu_i_br_sel(idu_1_idu_o_br_sel),
    .exu_o_exu_data(exu_1_exu_o_exu_data), .exu_o_rs2_data(exu_1_exu_o_rs2_data),
    .exu_o_branch_taken(exu_1_exu_o_branch_taken));
  memu memu_1 (
    .clk(clk), .rst(rst), .memu_i_addr(exu_1_exu_o_exu_data), .memu_i_data(exu_1_exu_o_rs2_data),
    .memu_i_is_store(idu_1_idu_o_is_store), .memu_i_fmt_sel(idu_1_idu_o_fmt_sel),
    .memu_i_drdata(biu_1_biu_o_drdata), .memu_o_data(memu_1_memu_o_data), .memu_o_daddr(memu_1_memu_o_daddr),
    .memu_o_dwmask(memu_1_memu_o_dwmask), .memu_o_dwdata(memu_1_memu_o_dwdata));
  wbu wbu_1 (
    .clk(clk), .rst(rst), .wbu_i_pc(ifu_1_ifu_o_pc), .wbu_i_exu_data(exu_1_exu_o_exu_data),
    .wbu_i_memu_data(memu_1_memu_o_data), .wbu_i_wb_sel(idu_1_idu_o_wb_sel),
    .wbu_o_wb_data(wbu_1_wbu_o_wb_data));

  // Other names for the same wires on the sheet: dtim_addr[31:0] = core_o_dtim_addr;
  //   dtim_rdata[31:0] = core_i_dtim_rdata; dtim_wdata[31:0] = core_o_dtim_wdata; dtim_wmask[3:0] = core_o_dtim_wmask;
  //   itim_addr[31:0] = core_o_itim_addr; itim_rdata[31:0] = core_i_itim_rdata; mmio_addr[31:0] = core_o_mmio_addr;
  //   mmio_rdata[31:0] = core_i_mmio_rdata; mmio_wdata[31:0] = core_o_mmio_wdata; mmio_wmask[3:0] = core_o_mmio_wmask
endmodule

module ifu (
  input  clk,
  input  rst,
  input  ifu_i_halt,
  input  ifu_i_is_jump,
  input  ifu_i_is_branch_taken,
  input  [31:0] ifu_i_pc_target,
  input  [31:0] ifu_i_idata,
  output [31:0] ifu_o_pc,
  output [31:0] ifu_o_inst,
  output [31:0] ifu_o_iaddr
);

  wire not_1_out, not_2_out, or_1_out;
  wire [31:0] adder_1_out, multiplexer_1_out;

  or or_1 (or_1_out, ifu_i_is_jump, ifu_i_is_branch_taken);
  Adder #(.width(32)) adder_1 (.a(ifu_o_iaddr), .b(32'h4), .out(adder_1_out));  // open: cin, cout
  Multiplexer #(.width(32)) multiplexer_1 (
    .in0(adder_1_out), .in1(ifu_i_pc_target), .out(multiplexer_1_out), .sel(or_1_out));
  Register #(.width(32)) pc (.D(multiplexer_1_out), .en(not_1_out), .clk(clk), .Q(ifu_o_iaddr), .clr(not_2_out));
  not not_1 (not_1_out, ifu_i_halt);
  not not_2 (not_2_out, rst);

  assign ifu_o_inst = ifu_i_idata;
  assign ifu_o_pc = ifu_o_iaddr;

  // Other names for the same wires on the sheet: halt = ifu_i_halt; inst[31:0] = ifu_i_idata;
  //   is_branch_taken = ifu_i_is_branch_taken; is_jump = ifu_i_is_jump; pc[31:0] = ifu_o_iaddr;
  //   pc_target[31:0] = ifu_i_pc_target
endmodule

module idu (
  input  clk,
  input  rst,
  input  [31:0] idu_i_inst,
  input  [31:0] idu_i_rd_data,
  output idu_o_is_jump,
  output [31:0] idu_o_rs1_data,
  output [31:0] idu_o_rs2_data,
  output [31:0] idu_o_imm,
  output [1:0] idu_o_a_sel,
  output [1:0] idu_o_b_sel,
  output [10:0] idu_o_alu_sel,
  output [3:0] idu_o_br_sel,
  output idu_o_is_store,
  output [4:0] idu_o_fmt_sel,
  output [2:0] idu_o_wb_sel
);

  wire and_1_out, and_2_out, and_3_out, and_4_out, and_5_out, and_6_out, and_7_out, and_8_out, and_9_out,
       and_10_out, and_11_out, and_12_out, and_13_out, and_14_out, and_15_out, and_16_out, and_17_out,
       and_18_out, and_19_out, and_20_out, and_21_out, and_22_out, and_23_out, and_24_out, and_25_out,
       and_27_out, and_28_out, not_1_out, not_2_out, not_3_out, not_4_out, not_5_out, not_6_out, not_7_out,
       not_8_out, not_9_out, not_10_out, not_11_out, not_12_out, not_13_out, not_14_out, not_15_out,
       opcode_is_alu_i, opcode_is_alu_iw, opcode_is_alu_r, opcode_is_alu_rw, opcode_is_auipc,
       opcode_is_fence, opcode_is_jal, opcode_is_jalr, opcode_is_load, opcode_is_lui, opcode_is_sys,
       opcode_is_type_i, opcode_is_type_r, opcode_is_type_u, or_6_out, or_15_out, rd_w_en;
  wire [2:0] multiplexer_3_out;
  wire [9:0] or_16_out;
  wire [10:0] bit_extender_5_out;
  wire [31:0] bit_extender_1_out, bit_extender_2_out, bit_extender_3_out, bit_extender_4_out;

  Decoder #(.enable("false"), .select(5)) decoder_1 (
    .out0(opcode_is_load), .out3(opcode_is_fence), .out4(opcode_is_alu_i), .out5(opcode_is_auipc),
    .out6(opcode_is_alu_iw), .out8(idu_o_is_store), .out10(opcode_is_alu_r), .out11(opcode_is_lui),
    .out12(opcode_is_alu_rw), .out24(idu_o_br_sel[0]), .out25(opcode_is_jalr), .out26(opcode_is_jal),
    .out28(opcode_is_sys), .sel(idu_i_inst[6:2]));  // open: out1, out2, out7, out9, out13, out14, out15, out16, out17, out18, out19, out20, out21, out22, out23, out27, out29, out30, out31
  or or_1 (opcode_is_type_r, opcode_is_alu_r, opcode_is_alu_rw);
  or or_2 (opcode_is_type_i, opcode_is_load, opcode_is_fence, opcode_is_alu_i, opcode_is_alu_iw, opcode_is_jalr, opcode_is_sys);
  or or_3 (opcode_is_type_u, opcode_is_auipc, opcode_is_lui);
  assign bit_extender_1_out = {{20{idu_i_inst[31]}}, idu_i_inst[31:20]};  // Bit_Extender bit_extender_1
  assign bit_extender_2_out = {{20{idu_i_inst[31]}}, {idu_i_inst[31:25], idu_i_inst[11:7]}};  // Bit_Extender bit_extender_2
  assign bit_extender_3_out = {{19{idu_i_inst[31]}}, {idu_i_inst[31], idu_i_inst[7], idu_i_inst[30:25], idu_i_inst[11:8], 1'b0}};  // Bit_Extender bit_extender_3
  assign bit_extender_4_out = {{11{idu_i_inst[31]}}, {idu_i_inst[31], idu_i_inst[19:12], idu_i_inst[20], idu_i_inst[30:21], 1'b0}};  // Bit_Extender bit_extender_4
  or or_4 (idu_o_is_jump, opcode_is_jal, opcode_is_jalr);
  or or_5 (rd_w_en, opcode_is_type_r, opcode_is_type_i, opcode_is_type_u, opcode_is_jal);
  or or_6 (or_6_out, opcode_is_auipc, idu_o_br_sel[0], opcode_is_jal);
  Multiplexer #(.width(2)) multiplexer_1 (.in0(2'b01), .in1(2'b10), .out(idu_o_a_sel), .sel(or_6_out));
  not not_1 (not_1_out, opcode_is_type_r);
  Multiplexer #(.width(2)) multiplexer_2 (.in0(2'b01), .in1(2'b10), .out(idu_o_b_sel), .sel(not_1_out));
  not not_2 (not_2_out, opcode_is_type_i);
  // Transmission_Gate #(.width(32)) transmission_1: pin names not known; wires that end beside it: bit_extender_1_out, not_2_out, opcode_is_type_i, idu_o_imm
  not not_3 (not_3_out, idu_o_is_store);
  // Transmission_Gate #(.width(32)) transmission_2: pin names not known; wires that end beside it: bit_extender_2_out, not_3_out, idu_o_is_store, idu_o_imm
  not not_4 (not_4_out, idu_o_br_sel[0]);
  // Transmission_Gate #(.width(32)) transmission_3: pin names not known; wires that end beside it: bit_extender_3_out, not_4_out, idu_o_br_sel[0], idu_o_imm
  not not_5 (not_5_out, opcode_is_type_u);
  // Transmission_Gate #(.width(32)) transmission_4: pin names not known; wires that end beside it: {idu_i_inst[31:12], {12{1'b0}}}, not_5_out, opcode_is_type_u, idu_o_imm
  not not_6 (not_6_out, opcode_is_jal);
  // Transmission_Gate #(.width(32)) transmission_5: pin names not known; wires that end beside it: bit_extender_4_out, not_6_out, opcode_is_jal, idu_o_imm
  and and_1 (and_1_out, idu_i_inst[12], idu_i_inst[13], idu_i_inst[14]);
  not not_7 (not_7_out, idu_i_inst[30]);
  and and_2 (and_2_out, ~idu_i_inst[12], idu_i_inst[13], idu_i_inst[14]);  // AND_Gate
  not not_8 (not_8_out, idu_i_inst[30]);
  and and_3 (and_3_out, opcode_is_alu_r, ~idu_i_inst[12], idu_i_inst[13]);  // AND_Gate
  and and_4 (and_4_out, ~idu_i_inst[12], ~idu_i_inst[13], idu_i_inst[14]);  // AND_Gate
  not not_9 (not_9_out, idu_i_inst[30]);
  and and_5 (and_5_out, idu_i_inst[12], idu_i_inst[13], ~idu_i_inst[14]);  // AND_Gate
  not not_10 (not_10_out, idu_i_inst[30]);
  and and_6 (and_6_out, ~idu_i_inst[12], idu_i_inst[13], ~idu_i_inst[14]);  // AND_Gate
  not not_11 (not_11_out, idu_i_inst[30]);
  and and_7 (and_7_out, ~idu_i_inst[12], idu_i_inst[13], ~idu_i_inst[14]);  // AND_Gate
  not not_12 (not_12_out, idu_i_inst[30]);
  and and_8 (and_8_out, idu_i_inst[12], ~idu_i_inst[13], ~idu_i_inst[14]);  // AND_Gate
  not not_13 (not_13_out, idu_i_inst[30]);
  and and_9 (and_9_out, ~idu_i_inst[12], ~idu_i_inst[13], ~idu_i_inst[14]);  // AND_Gate
  not not_14 (not_14_out, idu_i_inst[30]);
  and and_10 (and_10_out, and_1_out, opcode_is_alu_i);
  or or_7 (or_16_out[9], and_10_out, and_11_out);
  and and_11 (and_11_out, and_1_out, opcode_is_alu_r, not_7_out);
  and and_12 (and_12_out, and_2_out, opcode_is_alu_i);
  or or_8 (or_16_out[8], and_12_out, and_13_out);
  and and_13 (and_13_out, and_2_out, opcode_is_alu_r, not_8_out);
  and and_14 (and_14_out, and_3_out, idu_i_inst[14], opcode_is_alu_i);
  or or_9 (or_16_out[7], and_14_out, and_15_out);
  and and_15 (and_15_out, and_3_out, opcode_is_alu_r, idu_i_inst[14]);
  and and_16 (and_16_out, and_4_out, not_9_out, opcode_is_alu_i);
  or or_10 (or_16_out[6], and_16_out, and_17_out);
  and and_17 (and_17_out, and_4_out, opcode_is_alu_r, not_9_out);
  and and_18 (and_18_out, and_5_out, opcode_is_alu_i);
  or or_11 (or_16_out[5], and_18_out, and_19_out);
  and and_19 (and_19_out, and_5_out, opcode_is_alu_r, not_10_out);
  and and_20 (and_20_out, and_6_out, opcode_is_alu_i);
  or or_12 (or_16_out[4], and_20_out, and_21_out);
  and and_21 (and_21_out, and_6_out, opcode_is_alu_r, not_11_out);
  and and_22 (and_22_out, and_7_out, opcode_is_alu_i);
  or or_13 (or_16_out[3], and_22_out, and_23_out);
  and and_23 (and_23_out, and_7_out, opcode_is_alu_r, not_12_out);
  and and_24 (and_24_out, and_8_out, not_13_out, opcode_is_alu_i);
  or or_14 (or_16_out[2], and_24_out, and_25_out);
  and and_25 (and_25_out, and_8_out, opcode_is_alu_r, not_13_out);
  and and_26 (or_16_out[1], and_9_out, idu_i_inst[30]);
  and and_27 (and_27_out, and_9_out, opcode_is_alu_i);
  or or_15 (or_15_out, and_27_out, and_28_out);
  and and_28 (and_28_out, and_9_out, opcode_is_alu_r, not_14_out);
  idu_regfile idu_regfile_1 (
    .clk(clk), .idu_regfile_i_rs1_addr(idu_i_inst[19:15]), .idu_regfile_i_rs2_addr(idu_i_inst[24:20]),
    .idu_regfile_i_rd_addr(idu_i_inst[11:7]), .idu_regfile_i_rd_data(idu_i_rd_data),
    .idu_regfile_i_w_en(rd_w_en), .idu_regfile_o_rs1_data(idu_o_rs1_data),
    .idu_regfile_o_rs2_data(idu_o_rs2_data));
  or or_16 (or_16_out[0], or_15_out, opcode_is_auipc, opcode_is_jalr, opcode_is_load, opcode_is_jal, idu_o_br_sel[0], idu_o_is_store);
  and and_29 (idu_o_fmt_sel[3], idu_i_inst[12], idu_i_inst[13]);
  and and_30 (idu_o_fmt_sel[2], ~idu_i_inst[12], idu_i_inst[13]);  // AND_Gate
  and and_31 (idu_o_fmt_sel[1], idu_i_inst[12], ~idu_i_inst[13]);  // AND_Gate
  and and_32 (idu_o_fmt_sel[0], ~idu_i_inst[12], ~idu_i_inst[13]);  // AND_Gate
  not not_15 (not_15_out, idu_o_br_sel[0]);
  Multiplexer #(.width(3)) multiplexer_3 (.in0(3'b001), .in1(3'b010), .out(multiplexer_3_out), .sel(opcode_is_load));
  Multiplexer #(.width(3)) multiplexer_4 (
    .in0(multiplexer_3_out), .in1(3'b100), .out(idu_o_wb_sel), .sel(idu_o_is_jump));
  assign bit_extender_5_out = {{10{not_15_out}}, not_15_out};  // Bit_Extender bit_extender_5
  assign idu_o_alu_sel = bit_extender_5_out & {opcode_is_lui, or_16_out};  // AND_Gate and_33, 11 bits wide

  assign idu_o_br_sel[3:1] = idu_i_inst[14:12];
  assign idu_o_fmt_sel[4] = idu_i_inst[14];

  // Other names for the same wires on the sheet: inst[31:0] = idu_i_inst; rd_addr[4:0] = idu_i_inst[11:7];
  //   rs2_addr[4:0] = idu_i_inst[24:20]; funct7[6:0] = idu_i_inst[31:25]; rs1_addr[4:0] = idu_i_inst[19:15];
  //   a_sel[1:0] = idu_o_a_sel; alu_sel[10:0] = idu_o_alu_sel; b_sel[1:0] = idu_o_b_sel;
  //   br_sel[3:0] = {idu_i_inst[14:12], idu_o_br_sel[0]}; opcode_is_branch = idu_o_br_sel[0];
  //   opcode_is_type_b = idu_o_br_sel[0]; funct3[2:0] = idu_i_inst[14:12];
  //   fmt_sel[4:0] = {idu_i_inst[14], idu_o_fmt_sel[3:0]}; is_loadstore_byte = idu_o_fmt_sel[0];
  //   is_loadstore_half = idu_o_fmt_sel[1]; is_loadstore_word = idu_o_fmt_sel[2];
  //   is_loadstore_doubleword = idu_o_fmt_sel[3]; is_load_unsigned = idu_i_inst[14]; imm[31:0] = idu_o_imm;
  //   opcode[6:0] = idu_i_inst[6:0]; opcode_is_jump = idu_o_is_jump; opcode_is_type_j = opcode_is_jal;
  //   opcode_is_store = idu_o_is_store; opcode_is_type_s = idu_o_is_store; rd_data[31:0] = idu_i_rd_data;
  //   rs1_data[31:0] = idu_o_rs1_data; rs2_data[31:0] = idu_o_rs2_data; wb_sel[2:0] = idu_o_wb_sel
endmodule

module idu_regfile (
  input  clk,
  input  [4:0] idu_regfile_i_rs1_addr,
  input  [4:0] idu_regfile_i_rs2_addr,
  input  [4:0] idu_regfile_i_rd_addr,
  input  [31:0] idu_regfile_i_rd_data,
  input  idu_regfile_i_w_en,
  output [31:0] idu_regfile_o_rs1_data,
  output [31:0] idu_regfile_o_rs2_data
);

  wire and_1_out, and_2_out, and_3_out, and_4_out, and_5_out, and_6_out, and_7_out, and_8_out, and_9_out,
       and_10_out, and_11_out, and_12_out, and_13_out, and_14_out, and_15_out, and_16_out, and_17_out,
       and_18_out, and_19_out, and_20_out, and_21_out, and_22_out, and_23_out, and_24_out, and_25_out,
       and_26_out, and_27_out, and_28_out, and_29_out, and_30_out, and_31_out, and_32_out, and_49_out,
       and_50_out, and_51_out, and_52_out, and_53_out, and_54_out, and_55_out, and_56_out, and_57_out,
       and_58_out, and_59_out, and_60_out, and_61_out, and_62_out, and_63_out, and_64_out, and_65_out,
       and_66_out, and_67_out, and_68_out, and_69_out, and_70_out, and_71_out, and_72_out, and_73_out,
       and_74_out, and_75_out, and_76_out, and_77_out, and_78_out, and_79_out, and_80_out, and_97_out,
       and_98_out, and_99_out, and_100_out, and_101_out, and_102_out, and_103_out, and_104_out, and_105_out,
       and_106_out, and_107_out, and_108_out, and_109_out, and_110_out, and_111_out, and_112_out,
       and_113_out, and_114_out, and_115_out, and_116_out, and_117_out, and_118_out, and_119_out,
       and_120_out, and_121_out, and_122_out, and_123_out, and_124_out, and_125_out, and_126_out,
       and_127_out, and_128_out, and_145_out, and_146_out, and_147_out, and_148_out, and_149_out,
       and_150_out, and_151_out, and_152_out, and_153_out, and_154_out, and_155_out, and_156_out,
       and_157_out, and_158_out, and_159_out, and_160_out, and_161_out, and_162_out, and_163_out,
       and_164_out, and_165_out, and_166_out, and_167_out, and_168_out, and_169_out, and_170_out,
       and_171_out, and_172_out, and_173_out, and_174_out, and_175_out, and_176_out;
  wire [31:0] and_33_out, and_34_out, and_35_out, and_36_out, and_37_out, and_38_out, and_39_out, and_40_out,
       and_41_out, and_42_out, and_43_out, and_44_out, and_45_out, and_46_out, and_47_out, and_48_out,
       and_81_out, and_82_out, and_83_out, and_84_out, and_85_out, and_86_out, and_87_out, and_88_out,
       and_89_out, and_90_out, and_91_out, and_92_out, and_93_out, and_94_out, and_95_out, and_96_out,
       and_129_out, and_130_out, and_131_out, and_132_out, and_133_out, and_134_out, and_135_out,
       and_136_out, and_137_out, and_138_out, and_139_out, and_140_out, and_141_out, and_142_out,
       and_143_out, and_144_out, and_177_out, and_178_out, and_179_out, and_180_out, and_181_out,
       and_182_out, and_183_out, and_184_out, and_185_out, and_186_out, and_187_out, and_188_out,
       and_189_out, and_190_out, and_191_out, and_192_out, bit_extender_1_out, bit_extender_2_out,
       bit_extender_3_out, bit_extender_4_out, bit_extender_5_out, bit_extender_6_out, bit_extender_7_out,
       bit_extender_8_out, bit_extender_9_out, bit_extender_10_out, bit_extender_11_out, bit_extender_12_out,
       bit_extender_13_out, bit_extender_14_out, bit_extender_15_out, bit_extender_16_out,
       bit_extender_17_out, bit_extender_18_out, bit_extender_19_out, bit_extender_20_out,
       bit_extender_21_out, bit_extender_22_out, bit_extender_23_out, bit_extender_24_out,
       bit_extender_25_out, bit_extender_26_out, bit_extender_27_out, bit_extender_28_out,
       bit_extender_29_out, bit_extender_30_out, bit_extender_31_out, bit_extender_32_out,
       bit_extender_33_out, bit_extender_34_out, bit_extender_35_out, bit_extender_36_out,
       bit_extender_37_out, bit_extender_38_out, bit_extender_39_out, bit_extender_40_out,
       bit_extender_41_out, bit_extender_42_out, bit_extender_43_out, bit_extender_44_out,
       bit_extender_45_out, bit_extender_46_out, bit_extender_47_out, bit_extender_48_out,
       bit_extender_49_out, bit_extender_50_out, bit_extender_51_out, bit_extender_52_out,
       bit_extender_53_out, bit_extender_54_out, bit_extender_55_out, bit_extender_56_out,
       bit_extender_57_out, bit_extender_58_out, bit_extender_59_out, bit_extender_60_out,
       bit_extender_61_out, bit_extender_62_out, bit_extender_63_out, bit_extender_64_out, or_1_out,
       or_2_out, or_3_out, or_4_out, or_5_out, or_6_out, or_7_out, or_8_out, or_9_out, or_10_out, or_11_out,
       or_12_out, or_13_out, or_14_out, or_15_out, or_16_out, or_17_out, or_18_out, or_19_out, or_20_out,
       or_21_out, or_22_out, or_23_out, or_24_out, or_25_out, or_26_out, or_27_out, or_28_out, or_29_out,
       or_30_out, or_31_out, or_32_out, or_33_out, or_34_out, or_35_out, or_36_out, or_37_out, or_38_out,
       or_39_out, or_40_out, or_41_out, or_42_out, or_43_out, or_44_out, or_45_out, or_46_out, or_47_out,
       or_48_out, or_49_out, or_50_out, or_51_out, or_52_out, or_53_out, or_56_out, or_57_out, or_58_out,
       or_59_out, or_60_out, or_61_out, or_62_out, x0_q, x1_q, x2_q, x3_q, x4_q, x5_q, x6_q, x7_q, x8_q,
       x9_q, x10_q, x11_q, x12_q, x13_q, x14_q, x15_q, x16_q, x17_q, x18_q, x19_q, x20_q, x21_q, x22_q,
       x23_q, x24_q, x25_q, x26_q, x27_q, x28_q, x29_q, x30_q, x31_q;

  and and_1 (and_1_out, ~idu_regfile_i_rd_addr[4], ~idu_regfile_i_rd_addr[3], ~idu_regfile_i_rd_addr[2], ~idu_regfile_i_rd_addr[1], ~idu_regfile_i_rd_addr[0]);  // AND_Gate
  and and_2 (and_2_out, ~idu_regfile_i_rs1_addr[4], ~idu_regfile_i_rs1_addr[3], ~idu_regfile_i_rs1_addr[2], ~idu_regfile_i_rs1_addr[1], ~idu_regfile_i_rs1_addr[0]);  // AND_Gate
  and and_3 (and_3_out, ~idu_regfile_i_rs2_addr[4], ~idu_regfile_i_rs2_addr[3], ~idu_regfile_i_rs2_addr[2], ~idu_regfile_i_rs2_addr[1], ~idu_regfile_i_rs2_addr[0]);  // AND_Gate
  and and_4 (and_4_out, ~idu_regfile_i_rd_addr[4], ~idu_regfile_i_rd_addr[3], ~idu_regfile_i_rd_addr[2], ~idu_regfile_i_rd_addr[1], idu_regfile_i_rd_addr[0]);  // AND_Gate
  and and_5 (and_5_out, ~idu_regfile_i_rs1_addr[4], ~idu_regfile_i_rs1_addr[3], ~idu_regfile_i_rs1_addr[2], ~idu_regfile_i_rs1_addr[1], idu_regfile_i_rs1_addr[0]);  // AND_Gate
  and and_6 (and_6_out, ~idu_regfile_i_rs2_addr[4], ~idu_regfile_i_rs2_addr[3], ~idu_regfile_i_rs2_addr[2], ~idu_regfile_i_rs2_addr[1], idu_regfile_i_rs2_addr[0]);  // AND_Gate
  and and_7 (and_7_out, ~idu_regfile_i_rd_addr[4], ~idu_regfile_i_rd_addr[3], ~idu_regfile_i_rd_addr[2], idu_regfile_i_rd_addr[1], ~idu_regfile_i_rd_addr[0]);  // AND_Gate
  and and_8 (and_8_out, ~idu_regfile_i_rs1_addr[4], ~idu_regfile_i_rs1_addr[3], ~idu_regfile_i_rs1_addr[2], idu_regfile_i_rs1_addr[1], ~idu_regfile_i_rs1_addr[0]);  // AND_Gate
  and and_9 (and_9_out, ~idu_regfile_i_rs2_addr[4], ~idu_regfile_i_rs2_addr[3], ~idu_regfile_i_rs2_addr[2], idu_regfile_i_rs2_addr[1], ~idu_regfile_i_rs2_addr[0]);  // AND_Gate
  and and_10 (and_10_out, ~idu_regfile_i_rd_addr[4], ~idu_regfile_i_rd_addr[3], ~idu_regfile_i_rd_addr[2], idu_regfile_i_rd_addr[1], idu_regfile_i_rd_addr[0]);  // AND_Gate
  and and_11 (and_11_out, ~idu_regfile_i_rs1_addr[4], ~idu_regfile_i_rs1_addr[3], ~idu_regfile_i_rs1_addr[2], idu_regfile_i_rs1_addr[1], idu_regfile_i_rs1_addr[0]);  // AND_Gate
  and and_12 (and_12_out, ~idu_regfile_i_rs2_addr[4], ~idu_regfile_i_rs2_addr[3], ~idu_regfile_i_rs2_addr[2], idu_regfile_i_rs2_addr[1], idu_regfile_i_rs2_addr[0]);  // AND_Gate
  and and_13 (and_13_out, ~idu_regfile_i_rd_addr[4], ~idu_regfile_i_rd_addr[3], idu_regfile_i_rd_addr[2], ~idu_regfile_i_rd_addr[1], ~idu_regfile_i_rd_addr[0]);  // AND_Gate
  and and_14 (and_14_out, ~idu_regfile_i_rs1_addr[4], ~idu_regfile_i_rs1_addr[3], idu_regfile_i_rs1_addr[2], ~idu_regfile_i_rs1_addr[1], ~idu_regfile_i_rs1_addr[0]);  // AND_Gate
  and and_15 (and_15_out, ~idu_regfile_i_rs2_addr[4], ~idu_regfile_i_rs2_addr[3], idu_regfile_i_rs2_addr[2], ~idu_regfile_i_rs2_addr[1], ~idu_regfile_i_rs2_addr[0]);  // AND_Gate
  and and_16 (and_16_out, ~idu_regfile_i_rd_addr[4], ~idu_regfile_i_rd_addr[3], idu_regfile_i_rd_addr[2], ~idu_regfile_i_rd_addr[1], idu_regfile_i_rd_addr[0]);  // AND_Gate
  and and_17 (and_17_out, ~idu_regfile_i_rs1_addr[4], ~idu_regfile_i_rs1_addr[3], idu_regfile_i_rs1_addr[2], ~idu_regfile_i_rs1_addr[1], idu_regfile_i_rs1_addr[0]);  // AND_Gate
  and and_18 (and_18_out, ~idu_regfile_i_rs2_addr[4], ~idu_regfile_i_rs2_addr[3], idu_regfile_i_rs2_addr[2], ~idu_regfile_i_rs2_addr[1], idu_regfile_i_rs2_addr[0]);  // AND_Gate
  and and_19 (and_19_out, ~idu_regfile_i_rd_addr[4], ~idu_regfile_i_rd_addr[3], idu_regfile_i_rd_addr[2], idu_regfile_i_rd_addr[1], ~idu_regfile_i_rd_addr[0]);  // AND_Gate
  and and_20 (and_20_out, ~idu_regfile_i_rs1_addr[4], ~idu_regfile_i_rs1_addr[3], idu_regfile_i_rs1_addr[2], idu_regfile_i_rs1_addr[1], ~idu_regfile_i_rs1_addr[0]);  // AND_Gate
  and and_21 (and_21_out, ~idu_regfile_i_rs2_addr[4], ~idu_regfile_i_rs2_addr[3], idu_regfile_i_rs2_addr[2], idu_regfile_i_rs2_addr[1], ~idu_regfile_i_rs2_addr[0]);  // AND_Gate
  and and_22 (and_22_out, ~idu_regfile_i_rd_addr[4], ~idu_regfile_i_rd_addr[3], idu_regfile_i_rd_addr[2], idu_regfile_i_rd_addr[1], idu_regfile_i_rd_addr[0]);  // AND_Gate
  and and_23 (and_23_out, ~idu_regfile_i_rs1_addr[4], ~idu_regfile_i_rs1_addr[3], idu_regfile_i_rs1_addr[2], idu_regfile_i_rs1_addr[1], idu_regfile_i_rs1_addr[0]);  // AND_Gate
  and and_24 (and_24_out, ~idu_regfile_i_rs2_addr[4], ~idu_regfile_i_rs2_addr[3], idu_regfile_i_rs2_addr[2], idu_regfile_i_rs2_addr[1], idu_regfile_i_rs2_addr[0]);  // AND_Gate
  Register #(.width(32)) x0 (.D(idu_regfile_i_rd_data), .en(and_25_out), .clk(clk), .Q(x0_q));  // open: clr
  and and_25 (and_25_out, idu_regfile_i_w_en, and_1_out);
  Register #(.width(32)) x1 (.D(idu_regfile_i_rd_data), .en(and_26_out), .clk(clk), .Q(x1_q));  // open: clr
  and and_26 (and_26_out, idu_regfile_i_w_en, and_4_out);
  Register #(.width(32)) x2 (.D(idu_regfile_i_rd_data), .en(and_27_out), .clk(clk), .Q(x2_q));  // open: clr
  and and_27 (and_27_out, idu_regfile_i_w_en, and_7_out);
  Register #(.width(32)) x3 (.D(idu_regfile_i_rd_data), .en(and_28_out), .clk(clk), .Q(x3_q));  // open: clr
  and and_28 (and_28_out, idu_regfile_i_w_en, and_10_out);
  Register #(.width(32)) x4 (.D(idu_regfile_i_rd_data), .en(and_29_out), .clk(clk), .Q(x4_q));  // open: clr
  and and_29 (and_29_out, idu_regfile_i_w_en, and_13_out);
  Register #(.width(32)) x5 (.D(idu_regfile_i_rd_data), .en(and_30_out), .clk(clk), .Q(x5_q));  // open: clr
  and and_30 (and_30_out, idu_regfile_i_w_en, and_16_out);
  Register #(.width(32)) x6 (.D(idu_regfile_i_rd_data), .en(and_31_out), .clk(clk), .Q(x6_q));  // open: clr
  and and_31 (and_31_out, idu_regfile_i_w_en, and_19_out);
  Register #(.width(32)) x7 (.D(idu_regfile_i_rd_data), .en(and_32_out), .clk(clk), .Q(x7_q));  // open: clr
  and and_32 (and_32_out, idu_regfile_i_w_en, and_22_out);
  assign bit_extender_1_out = {{31{and_2_out}}, and_2_out};  // Bit_Extender bit_extender_1
  assign bit_extender_2_out = {{31{and_3_out}}, and_3_out};  // Bit_Extender bit_extender_2
  assign bit_extender_3_out = {{31{and_5_out}}, and_5_out};  // Bit_Extender bit_extender_3
  assign bit_extender_4_out = {{31{and_6_out}}, and_6_out};  // Bit_Extender bit_extender_4
  assign bit_extender_5_out = {{31{and_8_out}}, and_8_out};  // Bit_Extender bit_extender_5
  assign bit_extender_6_out = {{31{and_9_out}}, and_9_out};  // Bit_Extender bit_extender_6
  assign bit_extender_7_out = {{31{and_11_out}}, and_11_out};  // Bit_Extender bit_extender_7
  assign bit_extender_8_out = {{31{and_12_out}}, and_12_out};  // Bit_Extender bit_extender_8
  assign bit_extender_9_out = {{31{and_14_out}}, and_14_out};  // Bit_Extender bit_extender_9
  assign bit_extender_10_out = {{31{and_15_out}}, and_15_out};  // Bit_Extender bit_extender_10
  assign bit_extender_11_out = {{31{and_17_out}}, and_17_out};  // Bit_Extender bit_extender_11
  assign bit_extender_12_out = {{31{and_18_out}}, and_18_out};  // Bit_Extender bit_extender_12
  assign bit_extender_13_out = {{31{and_20_out}}, and_20_out};  // Bit_Extender bit_extender_13
  assign bit_extender_14_out = {{31{and_21_out}}, and_21_out};  // Bit_Extender bit_extender_14
  assign bit_extender_15_out = {{31{and_23_out}}, and_23_out};  // Bit_Extender bit_extender_15
  assign bit_extender_16_out = {{31{and_24_out}}, and_24_out};  // Bit_Extender bit_extender_16
  assign or_1_out = and_33_out | or_3_out;  // OR_Gate or_1, 32 bits wide
  assign and_33_out = x0_q & bit_extender_1_out;  // AND_Gate and_33, 32 bits wide
  assign or_2_out = and_34_out | or_4_out;  // OR_Gate or_2, 32 bits wide
  assign and_34_out = x0_q & bit_extender_2_out;  // AND_Gate and_34, 32 bits wide
  assign or_3_out = and_35_out | or_5_out;  // OR_Gate or_3, 32 bits wide
  assign and_35_out = x1_q & bit_extender_3_out;  // AND_Gate and_35, 32 bits wide
  assign or_4_out = and_36_out | or_6_out;  // OR_Gate or_4, 32 bits wide
  assign and_36_out = x1_q & bit_extender_4_out;  // AND_Gate and_36, 32 bits wide
  assign or_5_out = and_37_out | or_7_out;  // OR_Gate or_5, 32 bits wide
  assign and_37_out = x2_q & bit_extender_5_out;  // AND_Gate and_37, 32 bits wide
  assign or_6_out = and_38_out | or_8_out;  // OR_Gate or_6, 32 bits wide
  assign and_38_out = x2_q & bit_extender_6_out;  // AND_Gate and_38, 32 bits wide
  assign or_7_out = and_39_out | or_9_out;  // OR_Gate or_7, 32 bits wide
  assign and_39_out = x3_q & bit_extender_7_out;  // AND_Gate and_39, 32 bits wide
  assign or_8_out = and_40_out | or_10_out;  // OR_Gate or_8, 32 bits wide
  assign and_40_out = x3_q & bit_extender_8_out;  // AND_Gate and_40, 32 bits wide
  assign or_9_out = and_41_out | or_11_out;  // OR_Gate or_9, 32 bits wide
  assign and_41_out = x4_q & bit_extender_9_out;  // AND_Gate and_41, 32 bits wide
  assign or_10_out = and_42_out | or_12_out;  // OR_Gate or_10, 32 bits wide
  assign and_42_out = x4_q & bit_extender_10_out;  // AND_Gate and_42, 32 bits wide
  assign or_11_out = and_43_out | or_13_out;  // OR_Gate or_11, 32 bits wide
  assign and_43_out = x5_q & bit_extender_11_out;  // AND_Gate and_43, 32 bits wide
  assign or_12_out = and_44_out | or_14_out;  // OR_Gate or_12, 32 bits wide
  assign and_44_out = x5_q & bit_extender_12_out;  // AND_Gate and_44, 32 bits wide
  assign or_13_out = and_45_out | and_47_out;  // OR_Gate or_13, 32 bits wide
  assign and_45_out = x6_q & bit_extender_13_out;  // AND_Gate and_45, 32 bits wide
  assign or_14_out = and_46_out | and_48_out;  // OR_Gate or_14, 32 bits wide
  assign and_46_out = x6_q & bit_extender_14_out;  // AND_Gate and_46, 32 bits wide
  assign and_47_out = x7_q & bit_extender_15_out;  // AND_Gate and_47, 32 bits wide
  assign and_48_out = x7_q & bit_extender_16_out;  // AND_Gate and_48, 32 bits wide
  and and_49 (and_49_out, idu_regfile_i_w_en, and_50_out);
  and and_50 (and_50_out, ~idu_regfile_i_rd_addr[4], idu_regfile_i_rd_addr[3], ~idu_regfile_i_rd_addr[2], ~idu_regfile_i_rd_addr[1], ~idu_regfile_i_rd_addr[0]);  // AND_Gate
  and and_51 (and_51_out, ~idu_regfile_i_rs1_addr[4], idu_regfile_i_rs1_addr[3], ~idu_regfile_i_rs1_addr[2], ~idu_regfile_i_rs1_addr[1], ~idu_regfile_i_rs1_addr[0]);  // AND_Gate
  and and_52 (and_52_out, ~idu_regfile_i_rs2_addr[4], idu_regfile_i_rs2_addr[3], ~idu_regfile_i_rs2_addr[2], ~idu_regfile_i_rs2_addr[1], ~idu_regfile_i_rs2_addr[0]);  // AND_Gate
  and and_53 (and_53_out, idu_regfile_i_w_en, and_54_out);
  and and_54 (and_54_out, ~idu_regfile_i_rd_addr[4], idu_regfile_i_rd_addr[3], ~idu_regfile_i_rd_addr[2], ~idu_regfile_i_rd_addr[1], idu_regfile_i_rd_addr[0]);  // AND_Gate
  and and_55 (and_55_out, ~idu_regfile_i_rs1_addr[4], idu_regfile_i_rs1_addr[3], ~idu_regfile_i_rs1_addr[2], ~idu_regfile_i_rs1_addr[1], idu_regfile_i_rs1_addr[0]);  // AND_Gate
  and and_56 (and_56_out, ~idu_regfile_i_rs2_addr[4], idu_regfile_i_rs2_addr[3], ~idu_regfile_i_rs2_addr[2], ~idu_regfile_i_rs2_addr[1], idu_regfile_i_rs2_addr[0]);  // AND_Gate
  and and_57 (and_57_out, idu_regfile_i_w_en, and_58_out);
  and and_58 (and_58_out, ~idu_regfile_i_rd_addr[4], idu_regfile_i_rd_addr[3], ~idu_regfile_i_rd_addr[2], idu_regfile_i_rd_addr[1], ~idu_regfile_i_rd_addr[0]);  // AND_Gate
  and and_59 (and_59_out, ~idu_regfile_i_rs1_addr[4], idu_regfile_i_rs1_addr[3], ~idu_regfile_i_rs1_addr[2], idu_regfile_i_rs1_addr[1], ~idu_regfile_i_rs1_addr[0]);  // AND_Gate
  and and_60 (and_60_out, ~idu_regfile_i_rs2_addr[4], idu_regfile_i_rs2_addr[3], ~idu_regfile_i_rs2_addr[2], idu_regfile_i_rs2_addr[1], ~idu_regfile_i_rs2_addr[0]);  // AND_Gate
  and and_61 (and_61_out, idu_regfile_i_w_en, and_62_out);
  and and_62 (and_62_out, ~idu_regfile_i_rd_addr[4], idu_regfile_i_rd_addr[3], ~idu_regfile_i_rd_addr[2], idu_regfile_i_rd_addr[1], idu_regfile_i_rd_addr[0]);  // AND_Gate
  and and_63 (and_63_out, ~idu_regfile_i_rs1_addr[4], idu_regfile_i_rs1_addr[3], ~idu_regfile_i_rs1_addr[2], idu_regfile_i_rs1_addr[1], idu_regfile_i_rs1_addr[0]);  // AND_Gate
  and and_64 (and_64_out, ~idu_regfile_i_rs2_addr[4], idu_regfile_i_rs2_addr[3], ~idu_regfile_i_rs2_addr[2], idu_regfile_i_rs2_addr[1], idu_regfile_i_rs2_addr[0]);  // AND_Gate
  and and_65 (and_65_out, idu_regfile_i_w_en, and_66_out);
  and and_66 (and_66_out, ~idu_regfile_i_rd_addr[4], idu_regfile_i_rd_addr[3], idu_regfile_i_rd_addr[2], ~idu_regfile_i_rd_addr[1], ~idu_regfile_i_rd_addr[0]);  // AND_Gate
  and and_67 (and_67_out, ~idu_regfile_i_rs1_addr[4], idu_regfile_i_rs1_addr[3], idu_regfile_i_rs1_addr[2], ~idu_regfile_i_rs1_addr[1], ~idu_regfile_i_rs1_addr[0]);  // AND_Gate
  and and_68 (and_68_out, ~idu_regfile_i_rs2_addr[4], idu_regfile_i_rs2_addr[3], idu_regfile_i_rs2_addr[2], ~idu_regfile_i_rs2_addr[1], ~idu_regfile_i_rs2_addr[0]);  // AND_Gate
  and and_69 (and_69_out, idu_regfile_i_w_en, and_70_out);
  and and_70 (and_70_out, ~idu_regfile_i_rd_addr[4], idu_regfile_i_rd_addr[3], idu_regfile_i_rd_addr[2], ~idu_regfile_i_rd_addr[1], idu_regfile_i_rd_addr[0]);  // AND_Gate
  and and_71 (and_71_out, ~idu_regfile_i_rs1_addr[4], idu_regfile_i_rs1_addr[3], idu_regfile_i_rs1_addr[2], ~idu_regfile_i_rs1_addr[1], idu_regfile_i_rs1_addr[0]);  // AND_Gate
  and and_72 (and_72_out, ~idu_regfile_i_rs2_addr[4], idu_regfile_i_rs2_addr[3], idu_regfile_i_rs2_addr[2], ~idu_regfile_i_rs2_addr[1], idu_regfile_i_rs2_addr[0]);  // AND_Gate
  and and_73 (and_73_out, idu_regfile_i_w_en, and_74_out);
  and and_74 (and_74_out, ~idu_regfile_i_rd_addr[4], idu_regfile_i_rd_addr[3], idu_regfile_i_rd_addr[2], idu_regfile_i_rd_addr[1], ~idu_regfile_i_rd_addr[0]);  // AND_Gate
  and and_75 (and_75_out, ~idu_regfile_i_rs1_addr[4], idu_regfile_i_rs1_addr[3], idu_regfile_i_rs1_addr[2], idu_regfile_i_rs1_addr[1], ~idu_regfile_i_rs1_addr[0]);  // AND_Gate
  and and_76 (and_76_out, ~idu_regfile_i_rs2_addr[4], idu_regfile_i_rs2_addr[3], idu_regfile_i_rs2_addr[2], idu_regfile_i_rs2_addr[1], ~idu_regfile_i_rs2_addr[0]);  // AND_Gate
  and and_77 (and_77_out, idu_regfile_i_w_en, and_78_out);
  and and_78 (and_78_out, ~idu_regfile_i_rd_addr[4], idu_regfile_i_rd_addr[3], idu_regfile_i_rd_addr[2], idu_regfile_i_rd_addr[1], idu_regfile_i_rd_addr[0]);  // AND_Gate
  and and_79 (and_79_out, ~idu_regfile_i_rs1_addr[4], idu_regfile_i_rs1_addr[3], idu_regfile_i_rs1_addr[2], idu_regfile_i_rs1_addr[1], idu_regfile_i_rs1_addr[0]);  // AND_Gate
  and and_80 (and_80_out, ~idu_regfile_i_rs2_addr[4], idu_regfile_i_rs2_addr[3], idu_regfile_i_rs2_addr[2], idu_regfile_i_rs2_addr[1], idu_regfile_i_rs2_addr[0]);  // AND_Gate
  Register #(.width(32)) x8 (.D(idu_regfile_i_rd_data), .en(and_49_out), .clk(clk), .Q(x8_q));  // open: clr
  assign bit_extender_17_out = {{31{and_51_out}}, and_51_out};  // Bit_Extender bit_extender_17
  assign bit_extender_18_out = {{31{and_52_out}}, and_52_out};  // Bit_Extender bit_extender_18
  Register #(.width(32)) x9 (.D(idu_regfile_i_rd_data), .en(and_53_out), .clk(clk), .Q(x9_q));  // open: clr
  assign bit_extender_19_out = {{31{and_55_out}}, and_55_out};  // Bit_Extender bit_extender_19
  assign bit_extender_20_out = {{31{and_56_out}}, and_56_out};  // Bit_Extender bit_extender_20
  Register #(.width(32)) x10 (.D(idu_regfile_i_rd_data), .en(and_57_out), .clk(clk), .Q(x10_q));  // open: clr
  assign bit_extender_21_out = {{31{and_59_out}}, and_59_out};  // Bit_Extender bit_extender_21
  assign bit_extender_22_out = {{31{and_60_out}}, and_60_out};  // Bit_Extender bit_extender_22
  Register #(.width(32)) x11 (.D(idu_regfile_i_rd_data), .en(and_61_out), .clk(clk), .Q(x11_q));  // open: clr
  assign bit_extender_23_out = {{31{and_63_out}}, and_63_out};  // Bit_Extender bit_extender_23
  assign bit_extender_24_out = {{31{and_64_out}}, and_64_out};  // Bit_Extender bit_extender_24
  Register #(.width(32)) x12 (.D(idu_regfile_i_rd_data), .en(and_65_out), .clk(clk), .Q(x12_q));  // open: clr
  assign bit_extender_25_out = {{31{and_67_out}}, and_67_out};  // Bit_Extender bit_extender_25
  assign bit_extender_26_out = {{31{and_68_out}}, and_68_out};  // Bit_Extender bit_extender_26
  Register #(.width(32)) x13 (.D(idu_regfile_i_rd_data), .en(and_69_out), .clk(clk), .Q(x13_q));  // open: clr
  assign bit_extender_27_out = {{31{and_71_out}}, and_71_out};  // Bit_Extender bit_extender_27
  assign bit_extender_28_out = {{31{and_72_out}}, and_72_out};  // Bit_Extender bit_extender_28
  Register #(.width(32)) x14 (.D(idu_regfile_i_rd_data), .en(and_73_out), .clk(clk), .Q(x14_q));  // open: clr
  assign bit_extender_29_out = {{31{and_75_out}}, and_75_out};  // Bit_Extender bit_extender_29
  assign bit_extender_30_out = {{31{and_76_out}}, and_76_out};  // Bit_Extender bit_extender_30
  Register #(.width(32)) x15 (.D(idu_regfile_i_rd_data), .en(and_77_out), .clk(clk), .Q(x15_q));  // open: clr
  assign bit_extender_31_out = {{31{and_79_out}}, and_79_out};  // Bit_Extender bit_extender_31
  assign bit_extender_32_out = {{31{and_80_out}}, and_80_out};  // Bit_Extender bit_extender_32
  assign or_15_out = and_81_out | or_16_out;  // OR_Gate or_15, 32 bits wide
  assign and_81_out = x8_q & bit_extender_17_out;  // AND_Gate and_81, 32 bits wide
  assign and_82_out = x8_q & bit_extender_18_out;  // AND_Gate and_82, 32 bits wide
  assign or_16_out = and_83_out | or_17_out;  // OR_Gate or_16, 32 bits wide
  assign and_83_out = x9_q & bit_extender_19_out;  // AND_Gate and_83, 32 bits wide
  assign and_84_out = x9_q & bit_extender_20_out;  // AND_Gate and_84, 32 bits wide
  assign or_17_out = and_85_out | or_18_out;  // OR_Gate or_17, 32 bits wide
  assign and_85_out = x10_q & bit_extender_21_out;  // AND_Gate and_85, 32 bits wide
  assign and_86_out = x10_q & bit_extender_22_out;  // AND_Gate and_86, 32 bits wide
  assign or_18_out = and_87_out | or_19_out;  // OR_Gate or_18, 32 bits wide
  assign and_87_out = x11_q & bit_extender_23_out;  // AND_Gate and_87, 32 bits wide
  assign and_88_out = x11_q & bit_extender_24_out;  // AND_Gate and_88, 32 bits wide
  assign or_19_out = and_89_out | or_20_out;  // OR_Gate or_19, 32 bits wide
  assign and_89_out = x12_q & bit_extender_25_out;  // AND_Gate and_89, 32 bits wide
  assign and_90_out = x12_q & bit_extender_26_out;  // AND_Gate and_90, 32 bits wide
  assign or_20_out = and_91_out | or_21_out;  // OR_Gate or_20, 32 bits wide
  assign and_91_out = x13_q & bit_extender_27_out;  // AND_Gate and_91, 32 bits wide
  assign and_92_out = x13_q & bit_extender_28_out;  // AND_Gate and_92, 32 bits wide
  assign or_21_out = and_93_out | and_95_out;  // OR_Gate or_21, 32 bits wide
  assign and_93_out = x14_q & bit_extender_29_out;  // AND_Gate and_93, 32 bits wide
  assign and_94_out = x14_q & bit_extender_30_out;  // AND_Gate and_94, 32 bits wide
  assign and_95_out = x15_q & bit_extender_31_out;  // AND_Gate and_95, 32 bits wide
  assign and_96_out = x15_q & bit_extender_32_out;  // AND_Gate and_96, 32 bits wide
  assign or_22_out = and_82_out | or_23_out;  // OR_Gate or_22, 32 bits wide
  assign or_23_out = and_84_out | or_24_out;  // OR_Gate or_23, 32 bits wide
  assign or_24_out = and_86_out | or_25_out;  // OR_Gate or_24, 32 bits wide
  assign or_25_out = and_88_out | or_26_out;  // OR_Gate or_25, 32 bits wide
  assign or_26_out = and_90_out | or_27_out;  // OR_Gate or_26, 32 bits wide
  assign or_27_out = and_92_out | or_28_out;  // OR_Gate or_27, 32 bits wide
  assign or_28_out = and_94_out | and_96_out;  // OR_Gate or_28, 32 bits wide
  assign or_29_out = or_1_out | or_15_out;  // OR_Gate or_29, 32 bits wide
  assign or_30_out = or_2_out | or_22_out;  // OR_Gate or_30, 32 bits wide
  and and_97 (and_97_out, idu_regfile_i_rd_addr[4], ~idu_regfile_i_rd_addr[3], ~idu_regfile_i_rd_addr[2], ~idu_regfile_i_rd_addr[1], ~idu_regfile_i_rd_addr[0]);  // AND_Gate
  and and_98 (and_98_out, idu_regfile_i_rs1_addr[4], ~idu_regfile_i_rs1_addr[3], ~idu_regfile_i_rs1_addr[2], ~idu_regfile_i_rs1_addr[1], ~idu_regfile_i_rs1_addr[0]);  // AND_Gate
  and and_99 (and_99_out, idu_regfile_i_rs2_addr[4], ~idu_regfile_i_rs2_addr[3], ~idu_regfile_i_rs2_addr[2], ~idu_regfile_i_rs2_addr[1], ~idu_regfile_i_rs2_addr[0]);  // AND_Gate
  and and_100 (and_100_out, idu_regfile_i_rd_addr[4], ~idu_regfile_i_rd_addr[3], ~idu_regfile_i_rd_addr[2], ~idu_regfile_i_rd_addr[1], idu_regfile_i_rd_addr[0]);  // AND_Gate
  and and_101 (and_101_out, idu_regfile_i_rs1_addr[4], ~idu_regfile_i_rs1_addr[3], ~idu_regfile_i_rs1_addr[2], ~idu_regfile_i_rs1_addr[1], idu_regfile_i_rs1_addr[0]);  // AND_Gate
  and and_102 (and_102_out, idu_regfile_i_rs2_addr[4], ~idu_regfile_i_rs2_addr[3], ~idu_regfile_i_rs2_addr[2], ~idu_regfile_i_rs2_addr[1], idu_regfile_i_rs2_addr[0]);  // AND_Gate
  and and_103 (and_103_out, idu_regfile_i_rd_addr[4], ~idu_regfile_i_rd_addr[3], ~idu_regfile_i_rd_addr[2], idu_regfile_i_rd_addr[1], ~idu_regfile_i_rd_addr[0]);  // AND_Gate
  and and_104 (and_104_out, idu_regfile_i_rs1_addr[4], ~idu_regfile_i_rs1_addr[3], ~idu_regfile_i_rs1_addr[2], idu_regfile_i_rs1_addr[1], ~idu_regfile_i_rs1_addr[0]);  // AND_Gate
  and and_105 (and_105_out, idu_regfile_i_rs2_addr[4], ~idu_regfile_i_rs2_addr[3], ~idu_regfile_i_rs2_addr[2], idu_regfile_i_rs2_addr[1], ~idu_regfile_i_rs2_addr[0]);  // AND_Gate
  and and_106 (and_106_out, idu_regfile_i_rd_addr[4], ~idu_regfile_i_rd_addr[3], ~idu_regfile_i_rd_addr[2], idu_regfile_i_rd_addr[1], idu_regfile_i_rd_addr[0]);  // AND_Gate
  and and_107 (and_107_out, idu_regfile_i_rs1_addr[4], ~idu_regfile_i_rs1_addr[3], ~idu_regfile_i_rs1_addr[2], idu_regfile_i_rs1_addr[1], idu_regfile_i_rs1_addr[0]);  // AND_Gate
  and and_108 (and_108_out, idu_regfile_i_rs2_addr[4], ~idu_regfile_i_rs2_addr[3], ~idu_regfile_i_rs2_addr[2], idu_regfile_i_rs2_addr[1], idu_regfile_i_rs2_addr[0]);  // AND_Gate
  and and_109 (and_109_out, idu_regfile_i_rd_addr[4], ~idu_regfile_i_rd_addr[3], idu_regfile_i_rd_addr[2], ~idu_regfile_i_rd_addr[1], ~idu_regfile_i_rd_addr[0]);  // AND_Gate
  and and_110 (and_110_out, idu_regfile_i_rs1_addr[4], ~idu_regfile_i_rs1_addr[3], idu_regfile_i_rs1_addr[2], ~idu_regfile_i_rs1_addr[1], ~idu_regfile_i_rs1_addr[0]);  // AND_Gate
  and and_111 (and_111_out, idu_regfile_i_rs2_addr[4], ~idu_regfile_i_rs2_addr[3], idu_regfile_i_rs2_addr[2], ~idu_regfile_i_rs2_addr[1], ~idu_regfile_i_rs2_addr[0]);  // AND_Gate
  and and_112 (and_112_out, idu_regfile_i_rd_addr[4], ~idu_regfile_i_rd_addr[3], idu_regfile_i_rd_addr[2], ~idu_regfile_i_rd_addr[1], idu_regfile_i_rd_addr[0]);  // AND_Gate
  and and_113 (and_113_out, idu_regfile_i_rs1_addr[4], ~idu_regfile_i_rs1_addr[3], idu_regfile_i_rs1_addr[2], ~idu_regfile_i_rs1_addr[1], idu_regfile_i_rs1_addr[0]);  // AND_Gate
  and and_114 (and_114_out, idu_regfile_i_rs2_addr[4], ~idu_regfile_i_rs2_addr[3], idu_regfile_i_rs2_addr[2], ~idu_regfile_i_rs2_addr[1], idu_regfile_i_rs2_addr[0]);  // AND_Gate
  and and_115 (and_115_out, idu_regfile_i_rd_addr[4], ~idu_regfile_i_rd_addr[3], idu_regfile_i_rd_addr[2], idu_regfile_i_rd_addr[1], ~idu_regfile_i_rd_addr[0]);  // AND_Gate
  and and_116 (and_116_out, idu_regfile_i_rs1_addr[4], ~idu_regfile_i_rs1_addr[3], idu_regfile_i_rs1_addr[2], idu_regfile_i_rs1_addr[1], ~idu_regfile_i_rs1_addr[0]);  // AND_Gate
  and and_117 (and_117_out, idu_regfile_i_rs2_addr[4], ~idu_regfile_i_rs2_addr[3], idu_regfile_i_rs2_addr[2], idu_regfile_i_rs2_addr[1], ~idu_regfile_i_rs2_addr[0]);  // AND_Gate
  and and_118 (and_118_out, idu_regfile_i_rd_addr[4], ~idu_regfile_i_rd_addr[3], idu_regfile_i_rd_addr[2], idu_regfile_i_rd_addr[1], idu_regfile_i_rd_addr[0]);  // AND_Gate
  and and_119 (and_119_out, idu_regfile_i_rs1_addr[4], ~idu_regfile_i_rs1_addr[3], idu_regfile_i_rs1_addr[2], idu_regfile_i_rs1_addr[1], idu_regfile_i_rs1_addr[0]);  // AND_Gate
  and and_120 (and_120_out, idu_regfile_i_rs2_addr[4], ~idu_regfile_i_rs2_addr[3], idu_regfile_i_rs2_addr[2], idu_regfile_i_rs2_addr[1], idu_regfile_i_rs2_addr[0]);  // AND_Gate
  Register #(.width(32)) x16 (.D(idu_regfile_i_rd_data), .en(and_121_out), .clk(clk), .Q(x16_q));  // open: clr
  and and_121 (and_121_out, idu_regfile_i_w_en, and_97_out);
  Register #(.width(32)) x17 (.D(idu_regfile_i_rd_data), .en(and_122_out), .clk(clk), .Q(x17_q));  // open: clr
  and and_122 (and_122_out, idu_regfile_i_w_en, and_100_out);
  Register #(.width(32)) x18 (.D(idu_regfile_i_rd_data), .en(and_123_out), .clk(clk), .Q(x18_q));  // open: clr
  and and_123 (and_123_out, idu_regfile_i_w_en, and_103_out);
  Register #(.width(32)) x19 (.D(idu_regfile_i_rd_data), .en(and_124_out), .clk(clk), .Q(x19_q));  // open: clr
  and and_124 (and_124_out, idu_regfile_i_w_en, and_106_out);
  Register #(.width(32)) x20 (.D(idu_regfile_i_rd_data), .en(and_125_out), .clk(clk), .Q(x20_q));  // open: clr
  and and_125 (and_125_out, idu_regfile_i_w_en, and_109_out);
  Register #(.width(32)) x21 (.D(idu_regfile_i_rd_data), .en(and_126_out), .clk(clk), .Q(x21_q));  // open: clr
  and and_126 (and_126_out, idu_regfile_i_w_en, and_112_out);
  Register #(.width(32)) x22 (.D(idu_regfile_i_rd_data), .en(and_127_out), .clk(clk), .Q(x22_q));  // open: clr
  and and_127 (and_127_out, idu_regfile_i_w_en, and_115_out);
  Register #(.width(32)) x23 (.D(idu_regfile_i_rd_data), .en(and_128_out), .clk(clk), .Q(x23_q));  // open: clr
  and and_128 (and_128_out, idu_regfile_i_w_en, and_118_out);
  assign bit_extender_33_out = {{31{and_98_out}}, and_98_out};  // Bit_Extender bit_extender_33
  assign bit_extender_34_out = {{31{and_99_out}}, and_99_out};  // Bit_Extender bit_extender_34
  assign bit_extender_35_out = {{31{and_101_out}}, and_101_out};  // Bit_Extender bit_extender_35
  assign bit_extender_36_out = {{31{and_102_out}}, and_102_out};  // Bit_Extender bit_extender_36
  assign bit_extender_37_out = {{31{and_104_out}}, and_104_out};  // Bit_Extender bit_extender_37
  assign bit_extender_38_out = {{31{and_105_out}}, and_105_out};  // Bit_Extender bit_extender_38
  assign bit_extender_39_out = {{31{and_107_out}}, and_107_out};  // Bit_Extender bit_extender_39
  assign bit_extender_40_out = {{31{and_108_out}}, and_108_out};  // Bit_Extender bit_extender_40
  assign bit_extender_41_out = {{31{and_110_out}}, and_110_out};  // Bit_Extender bit_extender_41
  assign bit_extender_42_out = {{31{and_111_out}}, and_111_out};  // Bit_Extender bit_extender_42
  assign bit_extender_43_out = {{31{and_113_out}}, and_113_out};  // Bit_Extender bit_extender_43
  assign bit_extender_44_out = {{31{and_114_out}}, and_114_out};  // Bit_Extender bit_extender_44
  assign bit_extender_45_out = {{31{and_116_out}}, and_116_out};  // Bit_Extender bit_extender_45
  assign bit_extender_46_out = {{31{and_117_out}}, and_117_out};  // Bit_Extender bit_extender_46
  assign bit_extender_47_out = {{31{and_119_out}}, and_119_out};  // Bit_Extender bit_extender_47
  assign bit_extender_48_out = {{31{and_120_out}}, and_120_out};  // Bit_Extender bit_extender_48
  assign or_31_out = and_129_out | or_33_out;  // OR_Gate or_31, 32 bits wide
  assign and_129_out = x16_q & bit_extender_33_out;  // AND_Gate and_129, 32 bits wide
  assign or_32_out = and_130_out | or_34_out;  // OR_Gate or_32, 32 bits wide
  assign and_130_out = x16_q & bit_extender_34_out;  // AND_Gate and_130, 32 bits wide
  assign or_33_out = and_131_out | or_35_out;  // OR_Gate or_33, 32 bits wide
  assign and_131_out = x17_q & bit_extender_35_out;  // AND_Gate and_131, 32 bits wide
  assign or_34_out = and_132_out | or_36_out;  // OR_Gate or_34, 32 bits wide
  assign and_132_out = x17_q & bit_extender_36_out;  // AND_Gate and_132, 32 bits wide
  assign or_35_out = and_133_out | or_37_out;  // OR_Gate or_35, 32 bits wide
  assign and_133_out = x18_q & bit_extender_37_out;  // AND_Gate and_133, 32 bits wide
  assign or_36_out = and_134_out | or_38_out;  // OR_Gate or_36, 32 bits wide
  assign and_134_out = x18_q & bit_extender_38_out;  // AND_Gate and_134, 32 bits wide
  assign or_37_out = and_135_out | or_39_out;  // OR_Gate or_37, 32 bits wide
  assign and_135_out = x19_q & bit_extender_39_out;  // AND_Gate and_135, 32 bits wide
  assign or_38_out = and_136_out | or_40_out;  // OR_Gate or_38, 32 bits wide
  assign and_136_out = x19_q & bit_extender_40_out;  // AND_Gate and_136, 32 bits wide
  assign or_39_out = and_137_out | or_41_out;  // OR_Gate or_39, 32 bits wide
  assign and_137_out = x20_q & bit_extender_41_out;  // AND_Gate and_137, 32 bits wide
  assign or_40_out = and_138_out | or_42_out;  // OR_Gate or_40, 32 bits wide
  assign and_138_out = x20_q & bit_extender_42_out;  // AND_Gate and_138, 32 bits wide
  assign or_41_out = and_139_out | or_43_out;  // OR_Gate or_41, 32 bits wide
  assign and_139_out = x21_q & bit_extender_43_out;  // AND_Gate and_139, 32 bits wide
  assign or_42_out = and_140_out | or_44_out;  // OR_Gate or_42, 32 bits wide
  assign and_140_out = x21_q & bit_extender_44_out;  // AND_Gate and_140, 32 bits wide
  assign or_43_out = and_141_out | and_143_out;  // OR_Gate or_43, 32 bits wide
  assign and_141_out = x22_q & bit_extender_45_out;  // AND_Gate and_141, 32 bits wide
  assign or_44_out = and_142_out | and_144_out;  // OR_Gate or_44, 32 bits wide
  assign and_142_out = x22_q & bit_extender_46_out;  // AND_Gate and_142, 32 bits wide
  assign and_143_out = x23_q & bit_extender_47_out;  // AND_Gate and_143, 32 bits wide
  assign and_144_out = x23_q & bit_extender_48_out;  // AND_Gate and_144, 32 bits wide
  assign or_45_out = or_29_out | or_31_out;  // OR_Gate or_45, 32 bits wide
  assign or_46_out = or_30_out | or_32_out;  // OR_Gate or_46, 32 bits wide
  and and_145 (and_145_out, idu_regfile_i_w_en, and_146_out);
  and and_146 (and_146_out, idu_regfile_i_rd_addr[4], idu_regfile_i_rd_addr[3], ~idu_regfile_i_rd_addr[2], ~idu_regfile_i_rd_addr[1], ~idu_regfile_i_rd_addr[0]);  // AND_Gate
  and and_147 (and_147_out, idu_regfile_i_rs1_addr[4], idu_regfile_i_rs1_addr[3], ~idu_regfile_i_rs1_addr[2], ~idu_regfile_i_rs1_addr[1], ~idu_regfile_i_rs1_addr[0]);  // AND_Gate
  and and_148 (and_148_out, idu_regfile_i_rs2_addr[4], idu_regfile_i_rs2_addr[3], ~idu_regfile_i_rs2_addr[2], ~idu_regfile_i_rs2_addr[1], ~idu_regfile_i_rs2_addr[0]);  // AND_Gate
  and and_149 (and_149_out, idu_regfile_i_w_en, and_150_out);
  and and_150 (and_150_out, idu_regfile_i_rd_addr[4], idu_regfile_i_rd_addr[3], ~idu_regfile_i_rd_addr[2], ~idu_regfile_i_rd_addr[1], idu_regfile_i_rd_addr[0]);  // AND_Gate
  and and_151 (and_151_out, idu_regfile_i_rs1_addr[4], idu_regfile_i_rs1_addr[3], ~idu_regfile_i_rs1_addr[2], ~idu_regfile_i_rs1_addr[1], idu_regfile_i_rs1_addr[0]);  // AND_Gate
  and and_152 (and_152_out, idu_regfile_i_rs2_addr[4], idu_regfile_i_rs2_addr[3], ~idu_regfile_i_rs2_addr[2], ~idu_regfile_i_rs2_addr[1], idu_regfile_i_rs2_addr[0]);  // AND_Gate
  and and_153 (and_153_out, idu_regfile_i_w_en, and_154_out);
  and and_154 (and_154_out, idu_regfile_i_rd_addr[4], idu_regfile_i_rd_addr[3], ~idu_regfile_i_rd_addr[2], idu_regfile_i_rd_addr[1], ~idu_regfile_i_rd_addr[0]);  // AND_Gate
  and and_155 (and_155_out, idu_regfile_i_rs1_addr[4], idu_regfile_i_rs1_addr[3], ~idu_regfile_i_rs1_addr[2], idu_regfile_i_rs1_addr[1], ~idu_regfile_i_rs1_addr[0]);  // AND_Gate
  and and_156 (and_156_out, idu_regfile_i_rs2_addr[4], idu_regfile_i_rs2_addr[3], ~idu_regfile_i_rs2_addr[2], idu_regfile_i_rs2_addr[1], ~idu_regfile_i_rs2_addr[0]);  // AND_Gate
  and and_157 (and_157_out, idu_regfile_i_w_en, and_158_out);
  and and_158 (and_158_out, idu_regfile_i_rd_addr[4], idu_regfile_i_rd_addr[3], ~idu_regfile_i_rd_addr[2], idu_regfile_i_rd_addr[1], idu_regfile_i_rd_addr[0]);  // AND_Gate
  and and_159 (and_159_out, idu_regfile_i_rs1_addr[4], idu_regfile_i_rs1_addr[3], ~idu_regfile_i_rs1_addr[2], idu_regfile_i_rs1_addr[1], idu_regfile_i_rs1_addr[0]);  // AND_Gate
  and and_160 (and_160_out, idu_regfile_i_rs2_addr[4], idu_regfile_i_rs2_addr[3], ~idu_regfile_i_rs2_addr[2], idu_regfile_i_rs2_addr[1], idu_regfile_i_rs2_addr[0]);  // AND_Gate
  and and_161 (and_161_out, idu_regfile_i_w_en, and_162_out);
  and and_162 (and_162_out, idu_regfile_i_rd_addr[4], idu_regfile_i_rd_addr[3], idu_regfile_i_rd_addr[2], ~idu_regfile_i_rd_addr[1], ~idu_regfile_i_rd_addr[0]);  // AND_Gate
  and and_163 (and_163_out, idu_regfile_i_rs1_addr[4], idu_regfile_i_rs1_addr[3], idu_regfile_i_rs1_addr[2], ~idu_regfile_i_rs1_addr[1], ~idu_regfile_i_rs1_addr[0]);  // AND_Gate
  and and_164 (and_164_out, idu_regfile_i_rs2_addr[4], idu_regfile_i_rs2_addr[3], idu_regfile_i_rs2_addr[2], ~idu_regfile_i_rs2_addr[1], ~idu_regfile_i_rs2_addr[0]);  // AND_Gate
  and and_165 (and_165_out, idu_regfile_i_w_en, and_166_out);
  and and_166 (and_166_out, idu_regfile_i_rd_addr[4], idu_regfile_i_rd_addr[3], idu_regfile_i_rd_addr[2], ~idu_regfile_i_rd_addr[1], idu_regfile_i_rd_addr[0]);  // AND_Gate
  and and_167 (and_167_out, idu_regfile_i_rs1_addr[4], idu_regfile_i_rs1_addr[3], idu_regfile_i_rs1_addr[2], ~idu_regfile_i_rs1_addr[1], idu_regfile_i_rs1_addr[0]);  // AND_Gate
  and and_168 (and_168_out, idu_regfile_i_rs2_addr[4], idu_regfile_i_rs2_addr[3], idu_regfile_i_rs2_addr[2], ~idu_regfile_i_rs2_addr[1], idu_regfile_i_rs2_addr[0]);  // AND_Gate
  and and_169 (and_169_out, idu_regfile_i_w_en, and_170_out);
  and and_170 (and_170_out, idu_regfile_i_rd_addr[4], idu_regfile_i_rd_addr[3], idu_regfile_i_rd_addr[2], idu_regfile_i_rd_addr[1], ~idu_regfile_i_rd_addr[0]);  // AND_Gate
  and and_171 (and_171_out, idu_regfile_i_rs1_addr[4], idu_regfile_i_rs1_addr[3], idu_regfile_i_rs1_addr[2], idu_regfile_i_rs1_addr[1], ~idu_regfile_i_rs1_addr[0]);  // AND_Gate
  and and_172 (and_172_out, idu_regfile_i_rs2_addr[4], idu_regfile_i_rs2_addr[3], idu_regfile_i_rs2_addr[2], idu_regfile_i_rs2_addr[1], ~idu_regfile_i_rs2_addr[0]);  // AND_Gate
  and and_173 (and_173_out, idu_regfile_i_w_en, and_174_out);
  and and_174 (and_174_out, idu_regfile_i_rd_addr[4], idu_regfile_i_rd_addr[3], idu_regfile_i_rd_addr[2], idu_regfile_i_rd_addr[1], idu_regfile_i_rd_addr[0]);
  and and_175 (and_175_out, idu_regfile_i_rs1_addr[4], idu_regfile_i_rs1_addr[3], idu_regfile_i_rs1_addr[2], idu_regfile_i_rs1_addr[1], idu_regfile_i_rs1_addr[0]);
  and and_176 (and_176_out, idu_regfile_i_rs2_addr[4], idu_regfile_i_rs2_addr[3], idu_regfile_i_rs2_addr[2], idu_regfile_i_rs2_addr[1], idu_regfile_i_rs2_addr[0]);
  Register #(.width(32)) x24 (.D(idu_regfile_i_rd_data), .en(and_145_out), .clk(clk), .Q(x24_q));  // open: clr
  assign bit_extender_49_out = {{31{and_147_out}}, and_147_out};  // Bit_Extender bit_extender_49
  assign bit_extender_50_out = {{31{and_148_out}}, and_148_out};  // Bit_Extender bit_extender_50
  Register #(.width(32)) x25 (.D(idu_regfile_i_rd_data), .en(and_149_out), .clk(clk), .Q(x25_q));  // open: clr
  assign bit_extender_51_out = {{31{and_151_out}}, and_151_out};  // Bit_Extender bit_extender_51
  assign bit_extender_52_out = {{31{and_152_out}}, and_152_out};  // Bit_Extender bit_extender_52
  Register #(.width(32)) x26 (.D(idu_regfile_i_rd_data), .en(and_153_out), .clk(clk), .Q(x26_q));  // open: clr
  assign bit_extender_53_out = {{31{and_155_out}}, and_155_out};  // Bit_Extender bit_extender_53
  assign bit_extender_54_out = {{31{and_156_out}}, and_156_out};  // Bit_Extender bit_extender_54
  Register #(.width(32)) x27 (.D(idu_regfile_i_rd_data), .en(and_157_out), .clk(clk), .Q(x27_q));  // open: clr
  assign bit_extender_55_out = {{31{and_159_out}}, and_159_out};  // Bit_Extender bit_extender_55
  assign bit_extender_56_out = {{31{and_160_out}}, and_160_out};  // Bit_Extender bit_extender_56
  Register #(.width(32)) x28 (.D(idu_regfile_i_rd_data), .en(and_161_out), .clk(clk), .Q(x28_q));  // open: clr
  assign bit_extender_57_out = {{31{and_163_out}}, and_163_out};  // Bit_Extender bit_extender_57
  assign bit_extender_58_out = {{31{and_164_out}}, and_164_out};  // Bit_Extender bit_extender_58
  Register #(.width(32)) x29 (.D(idu_regfile_i_rd_data), .en(and_165_out), .clk(clk), .Q(x29_q));  // open: clr
  assign bit_extender_59_out = {{31{and_167_out}}, and_167_out};  // Bit_Extender bit_extender_59
  assign bit_extender_60_out = {{31{and_168_out}}, and_168_out};  // Bit_Extender bit_extender_60
  Register #(.width(32)) x30 (.D(idu_regfile_i_rd_data), .en(and_169_out), .clk(clk), .Q(x30_q));  // open: clr
  assign bit_extender_61_out = {{31{and_171_out}}, and_171_out};  // Bit_Extender bit_extender_61
  assign bit_extender_62_out = {{31{and_172_out}}, and_172_out};  // Bit_Extender bit_extender_62
  Register #(.width(32)) x31 (.D(idu_regfile_i_rd_data), .en(and_173_out), .clk(clk), .Q(x31_q));  // open: clr
  assign bit_extender_63_out = {{31{and_175_out}}, and_175_out};  // Bit_Extender bit_extender_63
  assign bit_extender_64_out = {{31{and_176_out}}, and_176_out};  // Bit_Extender bit_extender_64
  assign or_47_out = and_177_out | or_48_out;  // OR_Gate or_47, 32 bits wide
  assign and_177_out = x24_q & bit_extender_49_out;  // AND_Gate and_177, 32 bits wide
  assign and_178_out = x24_q & bit_extender_50_out;  // AND_Gate and_178, 32 bits wide
  assign or_48_out = and_179_out | or_49_out;  // OR_Gate or_48, 32 bits wide
  assign and_179_out = x25_q & bit_extender_51_out;  // AND_Gate and_179, 32 bits wide
  assign and_180_out = x25_q & bit_extender_52_out;  // AND_Gate and_180, 32 bits wide
  assign or_49_out = and_181_out | or_50_out;  // OR_Gate or_49, 32 bits wide
  assign and_181_out = x26_q & bit_extender_53_out;  // AND_Gate and_181, 32 bits wide
  assign and_182_out = x26_q & bit_extender_54_out;  // AND_Gate and_182, 32 bits wide
  assign or_50_out = and_183_out | or_51_out;  // OR_Gate or_50, 32 bits wide
  assign and_183_out = x27_q & bit_extender_55_out;  // AND_Gate and_183, 32 bits wide
  assign and_184_out = x27_q & bit_extender_56_out;  // AND_Gate and_184, 32 bits wide
  assign or_51_out = and_185_out | or_52_out;  // OR_Gate or_51, 32 bits wide
  assign and_185_out = x28_q & bit_extender_57_out;  // AND_Gate and_185, 32 bits wide
  assign and_186_out = x28_q & bit_extender_58_out;  // AND_Gate and_186, 32 bits wide
  assign or_52_out = and_187_out | or_53_out;  // OR_Gate or_52, 32 bits wide
  assign and_187_out = x29_q & bit_extender_59_out;  // AND_Gate and_187, 32 bits wide
  assign and_188_out = x29_q & bit_extender_60_out;  // AND_Gate and_188, 32 bits wide
  assign or_53_out = and_189_out | and_191_out;  // OR_Gate or_53, 32 bits wide
  assign and_189_out = x30_q & bit_extender_61_out;  // AND_Gate and_189, 32 bits wide
  assign and_190_out = x30_q & bit_extender_62_out;  // AND_Gate and_190, 32 bits wide
  assign and_191_out = x31_q & bit_extender_63_out;  // AND_Gate and_191, 32 bits wide
  assign and_192_out = x31_q & bit_extender_64_out;  // AND_Gate and_192, 32 bits wide
  assign idu_regfile_o_rs1_data = or_45_out | or_47_out;  // OR_Gate or_54, 32 bits wide
  assign idu_regfile_o_rs2_data = or_46_out | or_56_out;  // OR_Gate or_55, 32 bits wide
  assign or_56_out = and_178_out | or_57_out;  // OR_Gate or_56, 32 bits wide
  assign or_57_out = and_180_out | or_58_out;  // OR_Gate or_57, 32 bits wide
  assign or_58_out = and_182_out | or_59_out;  // OR_Gate or_58, 32 bits wide
  assign or_59_out = and_184_out | or_60_out;  // OR_Gate or_59, 32 bits wide
  assign or_60_out = and_186_out | or_61_out;  // OR_Gate or_60, 32 bits wide
  assign or_61_out = and_188_out | or_62_out;  // OR_Gate or_61, 32 bits wide
  assign or_62_out = and_190_out | and_192_out;  // OR_Gate or_62, 32 bits wide
endmodule

module exu (
  input  clk,
  input  rst,
  input  [31:0] exu_i_pc,
  input  [31:0] exu_i_rs1_data,
  input  [31:0] exu_i_rs2_data,
  input  [31:0] exu_i_imm,
  input  [1:0] exu_i_a_sel,
  input  [1:0] exu_i_b_sel,
  input  [10:0] exu_i_alu_sel,
  input  [3:0] exu_i_br_sel,
  output [31:0] exu_o_exu_data,
  output [31:0] exu_o_rs2_data,
  output exu_o_branch_taken
);

  wire adder_1_cout, br_eq, br_lt, comparator_1_lt, comparator_2_lt, comparator_3_lt, comparator_4_lt,
       multiplexer_2_out, not_1_out, not_2_out, not_3_out, not_4_out, not_5_out, not_6_out, not_7_out,
       not_8_out, not_9_out, not_10_out, not_11_out, not_12_out, not_13_out, not_14_out, not_15_out,
       xor_2_out;
  wire [31:0] adder_1_out, and_1_out, bit_extender_1_out, bit_extender_2_out, or_1_out, shifter_1_out,
       shifter_2_out, shifter_3_out, subtractor_1_out, transmission_2_p4, transmission_4_p4, xor_1_out;

  not not_1 (not_1_out, exu_i_a_sel[0]);
  // Transmission_Gate #(.width(32)) transmission_1: pin names not known; wires that end beside it: exu_i_rs1_data, not_1_out, exu_i_a_sel[0]
  not not_2 (not_2_out, exu_i_a_sel[1]);
  // Transmission_Gate #(.width(32)) transmission_2: pin names not known; wires that end beside it: exu_i_pc, not_2_out, exu_i_a_sel[1], transmission_2_p4
  not not_3 (not_3_out, exu_i_b_sel[0]);
  // Transmission_Gate #(.width(32)) transmission_3: pin names not known; wires that end beside it: exu_i_rs2_data, not_3_out, exu_i_b_sel[0]
  not not_4 (not_4_out, exu_i_b_sel[1]);
  // Transmission_Gate #(.width(32)) transmission_4: pin names not known; wires that end beside it: exu_i_imm, not_4_out, exu_i_b_sel[1], transmission_4_p4
  Adder #(.width(32)) adder_1 (
    .a(transmission_2_p4), .b(transmission_4_p4), .out(adder_1_out), .cout(adder_1_cout));  // open: cin
  Subtractor #(.width(32)) subtractor_1 (
    .a(transmission_2_p4), .b(transmission_4_p4), .out(subtractor_1_out), .bin(adder_1_cout));  // open: bout
  Shifter #(.width(32)) shifter_1 (.in(transmission_2_p4), .\dist (transmission_4_p4[4:0]), .out(shifter_1_out));
  assign bit_extender_1_out = {{31{comparator_1_lt}}, comparator_1_lt};  // Bit_Extender bit_extender_1
  Comparator #(.width(32)) comparator_1 (
    .a(transmission_2_p4), .b(transmission_4_p4), .lt(comparator_1_lt));  // open: gt, eq
  assign bit_extender_2_out = {{31{comparator_2_lt}}, comparator_2_lt};  // Bit_Extender bit_extender_2
  Comparator #(.mode("unsigned"), .width(32)) comparator_2 (
    .a(transmission_2_p4), .b(transmission_4_p4), .lt(comparator_2_lt));  // open: gt, eq
  assign xor_1_out = transmission_2_p4 ^ transmission_4_p4;  // XOR_Gate xor_1, 32 bits wide
  Shifter #(.shift("lr"), .width(32)) shifter_2 (
    .in(transmission_2_p4), .\dist (transmission_4_p4[4:0]), .out(shifter_2_out));
  Shifter #(.shift("ar"), .width(32)) shifter_3 (
    .in(transmission_2_p4), .\dist (transmission_4_p4[4:0]), .out(shifter_3_out));
  assign or_1_out = transmission_2_p4 | transmission_4_p4;  // OR_Gate or_1, 32 bits wide
  assign and_1_out = transmission_2_p4 & transmission_4_p4;  // AND_Gate and_1, 32 bits wide
  not not_5 (not_5_out, exu_i_alu_sel[0]);
  not not_6 (not_6_out, exu_i_alu_sel[1]);
  not not_7 (not_7_out, exu_i_alu_sel[2]);
  not not_8 (not_8_out, exu_i_alu_sel[3]);
  not not_9 (not_9_out, exu_i_alu_sel[4]);
  not not_10 (not_10_out, exu_i_alu_sel[5]);
  not not_11 (not_11_out, exu_i_alu_sel[6]);
  not not_12 (not_12_out, exu_i_alu_sel[7]);
  not not_13 (not_13_out, exu_i_alu_sel[8]);
  not not_14 (not_14_out, exu_i_alu_sel[9]);
  not not_15 (not_15_out, exu_i_alu_sel[10]);
  // Transmission_Gate #(.width(32)) transmission_5: pin names not known; wires that end beside it: adder_1_out, not_5_out, exu_i_alu_sel[0]
  // Transmission_Gate #(.width(32)) transmission_6: pin names not known; wires that end beside it: subtractor_1_out, not_6_out, exu_i_alu_sel[1]
  // Transmission_Gate #(.width(32)) transmission_7: pin names not known; wires that end beside it: shifter_1_out, not_7_out, exu_i_alu_sel[2]
  // Transmission_Gate #(.width(32)) transmission_8: pin names not known; wires that end beside it: bit_extender_1_out, not_8_out, exu_i_alu_sel[3]
  // Transmission_Gate #(.width(32)) transmission_9: pin names not known; wires that end beside it: bit_extender_2_out, not_9_out, exu_i_alu_sel[4]
  // Transmission_Gate #(.width(32)) transmission_10: pin names not known; wires that end beside it: xor_1_out, not_10_out, exu_i_alu_sel[5]
  // Transmission_Gate #(.width(32)) transmission_11: pin names not known; wires that end beside it: shifter_2_out, not_11_out, exu_i_alu_sel[6]
  // Transmission_Gate #(.width(32)) transmission_12: pin names not known; wires that end beside it: shifter_3_out, not_12_out, exu_i_alu_sel[7]
  // Transmission_Gate #(.width(32)) transmission_13: pin names not known; wires that end beside it: or_1_out, not_13_out, exu_i_alu_sel[8]
  // Transmission_Gate #(.width(32)) transmission_14: pin names not known; wires that end beside it: and_1_out, not_14_out, exu_i_alu_sel[9]
  // Transmission_Gate #(.width(32)) transmission_15: pin names not known; wires that end beside it: transmission_4_p4, not_15_out, exu_i_alu_sel[10], exu_o_exu_data
  Comparator #(.width(32)) comparator_3 (.a(exu_i_rs1_data), .b(exu_i_rs2_data), .lt(comparator_3_lt));  // open: gt, eq
  Comparator #(.mode("unsigned"), .width(32)) comparator_4 (
    .a(exu_i_rs1_data), .b(exu_i_rs2_data), .eq(br_eq), .lt(comparator_4_lt));  // open: gt
  Multiplexer multiplexer_1 (.in0(comparator_3_lt), .in1(comparator_4_lt), .out(br_lt), .sel(exu_i_br_sel[2]));
  Multiplexer multiplexer_2 (.in0(br_eq), .in1(br_lt), .out(multiplexer_2_out), .sel(exu_i_br_sel[3]));
  and and_2 (exu_o_branch_taken, exu_i_br_sel[0], xor_2_out);
  xor xor_2 (xor_2_out, exu_i_br_sel[1], multiplexer_2_out);

  assign exu_o_rs2_data = exu_i_rs2_data;

  // Other names for the same wires on the sheet: a_sel[1:0] = exu_i_a_sel; alu_data[31:0] = exu_o_exu_data;
  //   alu_sel[10:0] = exu_i_alu_sel; b_sel[1:0] = exu_i_b_sel; br_sel[3:0] = exu_i_br_sel;
  //   branch_taken = exu_o_branch_taken; imm[31:0] = exu_i_imm; pc[31:0] = exu_i_pc; rs1_data[31:0] = exu_i_rs1_data;
  //   rs2_data[31:0] = exu_i_rs2_data
endmodule

module memu (
  input  clk,
  input  rst,
  input  [31:0] memu_i_addr,
  input  [31:0] memu_i_data,
  input  memu_i_is_store,
  input  [4:0] memu_i_fmt_sel,
  input  [31:0] memu_i_drdata,
  output [31:0] memu_o_data,
  output [31:0] memu_o_daddr,
  output [3:0] memu_o_dwmask,
  output [31:0] memu_o_dwdata
);

  wire and_1_out, and_2_out, and_3_out, and_4_out, and_5_out, and_6_out, and_7_out, and_8_out, and_9_out,
       and_10_out, and_11_out, and_12_out, and_13_out, and_14_out, and_15_out, and_16_out, and_17_out,
       and_18_out, and_19_out, and_20_out, and_21_out, and_22_out, and_23_out, and_24_out, and_25_out,
       and_26_out, and_27_out, and_28_out, not_1_out, not_2_out, not_3_out, not_4_out, not_5_out, not_6_out,
       not_7_out, not_8_out, not_9_out, not_10_out, not_11_out, not_12_out, not_13_out, not_14_out,
       not_15_out, not_16_out, not_17_out, not_18_out, not_19_out, not_20_out, not_21_out, not_22_out,
       not_23_out, not_24_out, not_25_out, not_26_out, not_27_out, not_28_out, not_29_out, not_30_out,
       not_31_out, not_32_out, not_33_out, or_1_out, or_2_out, or_3_out, or_4_out, or_5_out, or_6_out,
       or_7_out, or_8_out, transmission_14_p1;
  wire [3:0] bit_extender_1_out, transmission_1_p4;
  wire [31:0] bit_extender_2_out, bit_extender_3_out, bit_extender_4_out, bit_extender_5_out,
       bit_extender_6_out, bit_extender_7_out, bit_extender_8_out, bit_extender_9_out, bit_extender_10_out,
       bit_extender_11_out, bit_extender_12_out, bit_extender_13_out, shifter_1_out, shifter_2_out,
       shifter_3_out;

  and and_1 (and_1_out, ~memu_i_addr[0], ~memu_i_addr[1]);  // AND_Gate
  and and_2 (and_2_out, ~memu_i_addr[0], memu_i_addr[1]);  // AND_Gate
  and and_3 (and_3_out, memu_i_addr[0], ~memu_i_addr[1]);  // AND_Gate
  and and_4 (and_4_out, memu_i_addr[0], memu_i_addr[1]);
  or or_1 (or_1_out, and_1_out, and_2_out);
  or or_2 (or_2_out, and_3_out, and_4_out);
  or or_3 (or_3_out, and_1_out, and_2_out);
  or or_4 (or_4_out, and_3_out, and_4_out);
  or or_5 (or_5_out, and_1_out, and_2_out);
  or or_6 (or_6_out, and_3_out, and_4_out);
  or or_7 (or_7_out, and_1_out, and_2_out);
  or or_8 (or_8_out, and_3_out, and_4_out);
  and and_5 (and_5_out, memu_i_fmt_sel[1], or_1_out);
  and and_6 (and_6_out, memu_i_fmt_sel[1], or_2_out);
  and and_7 (and_7_out, memu_i_fmt_sel[0], and_1_out);
  and and_8 (and_8_out, memu_i_fmt_sel[0], and_2_out);
  and and_9 (and_9_out, memu_i_fmt_sel[0], and_3_out);
  and and_10 (and_10_out, memu_i_fmt_sel[0], and_4_out);
  and and_11 (and_11_out, memu_i_fmt_sel[1], or_3_out);
  and and_12 (and_12_out, memu_i_fmt_sel[1], or_4_out);
  and and_13 (and_13_out, memu_i_fmt_sel[0], and_1_out);
  and and_14 (and_14_out, memu_i_fmt_sel[0], and_2_out);
  and and_15 (and_15_out, memu_i_fmt_sel[0], and_3_out);
  and and_16 (and_16_out, memu_i_fmt_sel[0], and_4_out);
  not not_1 (not_1_out, memu_i_fmt_sel[4]);
  not not_2 (not_2_out, memu_i_fmt_sel[4]);
  not not_3 (not_3_out, memu_i_fmt_sel[4]);
  not not_4 (not_4_out, memu_i_fmt_sel[4]);
  not not_5 (not_5_out, memu_i_fmt_sel[4]);
  not not_6 (not_6_out, memu_i_fmt_sel[4]);
  not not_7 (not_7_out, memu_i_fmt_sel[2]);
  // Transmission_Gate #(.width(4)) transmission_1: pin names not known; wires that end beside it: 4'b1111, not_7_out, memu_i_fmt_sel[2], transmission_1_p4
  not not_8 (not_8_out, and_5_out);
  // Transmission_Gate #(.width(4)) transmission_2: pin names not known; wires that end beside it: 4'b0011, not_8_out, and_5_out, transmission_1_p4
  not not_9 (not_9_out, and_6_out);
  // Transmission_Gate #(.width(4)) transmission_3: pin names not known; wires that end beside it: 4'b1100, not_9_out, and_6_out, transmission_1_p4
  not not_10 (not_10_out, and_7_out);
  // Transmission_Gate #(.width(4)) transmission_4: pin names not known; wires that end beside it: 4'b0001, not_10_out, and_7_out, transmission_1_p4
  not not_11 (not_11_out, and_8_out);
  // Transmission_Gate #(.width(4)) transmission_5: pin names not known; wires that end beside it: 4'b0010, not_11_out, and_8_out, transmission_1_p4
  not not_12 (not_12_out, and_9_out);
  // Transmission_Gate #(.width(4)) transmission_6: pin names not known; wires that end beside it: 4'b0100, not_12_out, and_9_out, transmission_1_p4
  not not_13 (not_13_out, and_10_out);
  // Transmission_Gate #(.width(4)) transmission_7: pin names not known; wires that end beside it: 4'b1000, not_13_out, and_10_out, transmission_1_p4
  Shifter #(.width(32)) shifter_1 (.in(memu_i_data), .\dist (5'b10000), .out(shifter_1_out));
  Shifter #(.width(32)) shifter_2 (.in(memu_i_data), .\dist (5'b01000), .out(shifter_2_out));
  Shifter #(.width(32)) shifter_3 (.in(memu_i_data), .\dist (5'b10000), .out(shifter_3_out));
  Shifter #(.width(32)) shifter_4 (.in(memu_i_data), .\dist (5'b11000));  // open: out
  and and_17 (and_17_out, memu_i_fmt_sel[1], not_1_out, or_5_out);
  and and_18 (and_18_out, memu_i_fmt_sel[1], not_2_out, or_6_out);
  and and_19 (and_19_out, memu_i_fmt_sel[1], memu_i_fmt_sel[4], or_7_out);
  and and_20 (and_20_out, memu_i_fmt_sel[1], memu_i_fmt_sel[4], or_8_out);
  and and_21 (and_21_out, memu_i_fmt_sel[0], not_3_out, and_1_out);
  and and_22 (and_22_out, memu_i_fmt_sel[0], not_4_out, and_2_out);
  and and_23 (and_23_out, memu_i_fmt_sel[0], not_5_out, and_3_out);
  and and_24 (and_24_out, memu_i_fmt_sel[0], not_6_out, and_4_out);
  and and_25 (and_25_out, memu_i_fmt_sel[0], memu_i_fmt_sel[4], and_1_out);
  and and_26 (and_26_out, memu_i_fmt_sel[0], memu_i_fmt_sel[4], and_2_out);
  and and_27 (and_27_out, memu_i_fmt_sel[0], memu_i_fmt_sel[4], and_3_out);
  and and_28 (and_28_out, memu_i_fmt_sel[0], memu_i_fmt_sel[4], and_4_out);
  assign bit_extender_1_out = {{3{memu_i_is_store}}, memu_i_is_store};  // Bit_Extender bit_extender_1
  assign memu_o_dwmask = bit_extender_1_out & transmission_1_p4;  // AND_Gate and_29, 4 bits wide
  not not_14 (not_14_out, memu_i_fmt_sel[2]);
  // Transmission_Gate #(.width(32)) transmission_8: pin names not known; wires that end beside it: memu_i_data, not_14_out, memu_i_fmt_sel[2], memu_o_dwdata
  not not_15 (not_15_out, and_11_out);
  // Transmission_Gate #(.width(32)) transmission_9: pin names not known; wires that end beside it: memu_i_data, not_15_out, and_11_out, memu_o_dwdata
  not not_16 (not_16_out, and_12_out);
  // Transmission_Gate #(.width(32)) transmission_10: pin names not known; wires that end beside it: shifter_1_out, not_16_out, and_12_out, memu_o_dwdata
  not not_17 (not_17_out, and_13_out);
  // Transmission_Gate #(.width(32)) transmission_11: pin names not known; wires that end beside it: memu_i_data, not_17_out, and_13_out, memu_o_dwdata
  not not_18 (not_18_out, and_14_out);
  // Transmission_Gate #(.width(32)) transmission_12: pin names not known; wires that end beside it: shifter_2_out, not_18_out, and_14_out, memu_o_dwdata
  not not_19 (not_19_out, and_15_out);
  // Transmission_Gate #(.width(32)) transmission_13: pin names not known; wires that end beside it: shifter_3_out, not_19_out, and_15_out, memu_o_dwdata
  not not_20 (not_20_out, and_16_out);
  // Transmission_Gate #(.width(32)) transmission_14: pin names not known; wires that end beside it: transmission_14_p1, transmission_14_p1, not_20_out, and_16_out, memu_o_dwdata
  not not_21 (not_21_out, memu_i_fmt_sel[2]);
  not not_22 (not_22_out, and_17_out);
  assign bit_extender_2_out = {{16{memu_i_drdata[15]}}, memu_i_drdata[15:0]};  // Bit_Extender bit_extender_2
  not not_23 (not_23_out, and_18_out);
  assign bit_extender_3_out = {{16{memu_i_drdata[31]}}, memu_i_drdata[31:16]};  // Bit_Extender bit_extender_3
  not not_24 (not_24_out, and_19_out);
  assign bit_extender_4_out = {{16{1'b0}}, memu_i_drdata[15:0]};  // Bit_Extender bit_extender_4
  not not_25 (not_25_out, and_20_out);
  assign bit_extender_5_out = {{16{1'b0}}, memu_i_drdata[31:16]};  // Bit_Extender bit_extender_5
  not not_26 (not_26_out, and_21_out);
  assign bit_extender_6_out = {{24{memu_i_drdata[7]}}, memu_i_drdata[7:0]};  // Bit_Extender bit_extender_6
  not not_27 (not_27_out, and_22_out);
  assign bit_extender_7_out = {{24{memu_i_drdata[15]}}, memu_i_drdata[15:8]};  // Bit_Extender bit_extender_7
  not not_28 (not_28_out, and_23_out);
  assign bit_extender_8_out = {{24{memu_i_drdata[23]}}, memu_i_drdata[23:16]};  // Bit_Extender bit_extender_8
  not not_29 (not_29_out, and_24_out);
  assign bit_extender_9_out = {{24{memu_i_drdata[31]}}, memu_i_drdata[31:24]};  // Bit_Extender bit_extender_9
  not not_30 (not_30_out, and_25_out);
  assign bit_extender_10_out = {{24{1'b0}}, memu_i_drdata[7:0]};  // Bit_Extender bit_extender_10
  not not_31 (not_31_out, and_26_out);
  assign bit_extender_11_out = {{24{1'b0}}, memu_i_drdata[15:8]};  // Bit_Extender bit_extender_11
  not not_32 (not_32_out, and_27_out);
  assign bit_extender_12_out = {{24{1'b0}}, memu_i_drdata[23:16]};  // Bit_Extender bit_extender_12
  not not_33 (not_33_out, and_28_out);
  assign bit_extender_13_out = {{24{1'b0}}, memu_i_drdata[31:24]};  // Bit_Extender bit_extender_13
  // Transmission_Gate #(.width(32)) transmission_15: pin names not known; wires that end beside it: memu_i_drdata, not_21_out, memu_i_fmt_sel[2], memu_o_data
  // Transmission_Gate #(.width(32)) transmission_16: pin names not known; wires that end beside it: bit_extender_2_out, not_22_out, and_17_out, memu_o_data
  // Transmission_Gate #(.width(32)) transmission_17: pin names not known; wires that end beside it: bit_extender_3_out, not_23_out, and_18_out, memu_o_data
  // Transmission_Gate #(.width(32)) transmission_18: pin names not known; wires that end beside it: bit_extender_4_out, not_24_out, and_19_out, memu_o_data
  // Transmission_Gate #(.width(32)) transmission_19: pin names not known; wires that end beside it: bit_extender_5_out, not_25_out, and_20_out, memu_o_data
  // Transmission_Gate #(.width(32)) transmission_20: pin names not known; wires that end beside it: bit_extender_6_out, not_26_out, and_21_out, memu_o_data
  // Transmission_Gate #(.width(32)) transmission_21: pin names not known; wires that end beside it: bit_extender_7_out, not_27_out, and_22_out, memu_o_data
  // Transmission_Gate #(.width(32)) transmission_22: pin names not known; wires that end beside it: bit_extender_8_out, not_28_out, and_23_out, memu_o_data
  // Transmission_Gate #(.width(32)) transmission_23: pin names not known; wires that end beside it: bit_extender_9_out, not_29_out, and_24_out, memu_o_data
  // Transmission_Gate #(.width(32)) transmission_24: pin names not known; wires that end beside it: bit_extender_10_out, not_30_out, and_25_out, memu_o_data
  // Transmission_Gate #(.width(32)) transmission_25: pin names not known; wires that end beside it: bit_extender_11_out, not_31_out, and_26_out, memu_o_data
  // Transmission_Gate #(.width(32)) transmission_26: pin names not known; wires that end beside it: bit_extender_12_out, not_32_out, and_27_out, memu_o_data
  // Transmission_Gate #(.width(32)) transmission_27: pin names not known; wires that end beside it: bit_extender_13_out, not_33_out, and_28_out, memu_o_data

  assign memu_o_daddr = memu_i_addr;

  // Other names for the same wires on the sheet: addr[31:0] = memu_i_addr; drdata[31:0] = memu_i_drdata;
  //   dwdata[31:0] = memu_o_dwdata; dwmask[3:0] = memu_o_dwmask; fmt_sel[4:0] = memu_i_fmt_sel;
  //   is_store = memu_i_is_store; rdata[31:0] = memu_o_data; wdata[31:0] = memu_i_data
endmodule

module wbu (
  input  clk,
  input  rst,
  input  [31:0] wbu_i_pc,
  input  [31:0] wbu_i_exu_data,
  input  [31:0] wbu_i_memu_data,
  input  [2:0] wbu_i_wb_sel,
  output [31:0] wbu_o_wb_data
);

  wire not_1_out, not_2_out, not_3_out;
  wire [31:0] adder_1_out;

  Adder #(.width(32)) adder_1 (.a(wbu_i_pc), .b(32'h4), .out(adder_1_out));  // open: cin, cout
  not not_1 (not_1_out, wbu_i_wb_sel[0]);
  not not_2 (not_2_out, wbu_i_wb_sel[1]);
  not not_3 (not_3_out, wbu_i_wb_sel[2]);
  // Transmission_Gate #(.width(32)) transmission_1: pin names not known; wires that end beside it: wbu_i_exu_data, not_1_out, wbu_i_wb_sel[0], wbu_o_wb_data
  // Transmission_Gate #(.width(32)) transmission_2: pin names not known; wires that end beside it: wbu_i_memu_data, not_2_out, wbu_i_wb_sel[1], wbu_o_wb_data
  // Transmission_Gate #(.width(32)) transmission_3: pin names not known; wires that end beside it: adder_1_out, not_3_out, wbu_i_wb_sel[2], wbu_o_wb_data

  // Other names for the same wires on the sheet: exu_data[31:0] = wbu_i_exu_data; memu_data[31:0] = wbu_i_memu_data;
  //   pc[31:0] = wbu_i_pc; wb_data[31:0] = wbu_o_wb_data; wb_sel[2:0] = wbu_i_wb_sel
endmodule

module biu (
  input  clk,
  input  rst,
  input  [31:0] biu_i_iaddr,
  input  [31:0] biu_i_daddr,
  input  [3:0] biu_i_dwmask,
  input  [31:0] biu_i_dwdata,
  input  [31:0] biu_i_itim_rdata,
  input  [31:0] biu_i_dtim_rdata,
  input  [31:0] biu_i_mmio_rdata,
  output biu_o_halt,
  output [31:0] biu_o_idata,
  output [31:0] biu_o_drdata,
  output [31:0] biu_o_itim_addr,
  output [31:0] biu_o_dtim_addr,
  output [3:0] biu_o_dtim_wmask,
  output [31:0] biu_o_dtim_wdata,
  output [31:0] biu_o_mmio_addr,
  output [3:0] biu_o_mmio_wmask,
  output [31:0] biu_o_mmio_wdata
);

  wire comparator_1_eq, comparator_1_gt, comparator_2_eq, comparator_2_gt, comparator_2_lt, comparator_3_eq,
       comparator_3_gt, comparator_3_lt, comparator_4_eq, comparator_4_gt, comparator_4_lt, is_dtim_addr,
       is_itim_addr, is_mmio_addr, or_1_out, or_2_out, or_3_out;
  wire [31:0] multiplexer_3_out, multiplexer_4_out;

  Subtractor #(.width(32)) subtractor_1 (.a(biu_i_daddr), .b(32'h1000), .out(biu_o_dtim_addr));  // open: bin, bout
  Multiplexer #(.width(4)) multiplexer_1 (
    .in0(biu_i_dwmask), .in1(4'b0000), .out(biu_o_dtim_wmask), .sel(is_dtim_addr));
  Subtractor #(.width(32)) subtractor_2 (.a(biu_i_daddr), .b(32'h2000), .out(biu_o_mmio_addr));  // open: bin, bout
  Multiplexer #(.width(4)) multiplexer_2 (
    .in0(biu_i_dwmask), .in1(4'b0000), .out(biu_o_mmio_wmask), .sel(is_mmio_addr));
  Multiplexer #(.width(32)) multiplexer_3 (
    .in0(32'hcccccccc), .in1(biu_i_mmio_rdata), .out(multiplexer_3_out), .sel(is_mmio_addr));
  Multiplexer #(.width(32)) multiplexer_4 (
    .in0(multiplexer_3_out), .in1(biu_i_dtim_rdata), .out(multiplexer_4_out), .sel(is_dtim_addr));
  or or_1 (or_1_out, comparator_1_gt, comparator_1_eq);
  Comparator #(.mode("unsigned"), .width(32)) comparator_1 (
    .a(biu_i_daddr), .b({32{1'b0}}), .gt(comparator_1_gt), .eq(comparator_1_eq));  // open: lt
  or or_2 (or_2_out, comparator_2_gt, comparator_2_eq);
  Comparator #(.mode("unsigned"), .width(32)) comparator_2 (
    .a(biu_i_daddr), .b(32'h1000), .gt(comparator_2_gt), .eq(comparator_2_eq), .lt(comparator_2_lt));
  or or_3 (or_3_out, comparator_3_gt, comparator_3_eq);
  Comparator #(.mode("unsigned"), .width(32)) comparator_3 (
    .a(biu_i_daddr), .b(32'h2000), .gt(comparator_3_gt), .eq(comparator_3_eq), .lt(comparator_3_lt));
  // OR_Gate or_4 has open pins: in0=comparator_4_gt, in1=comparator_4_eq, out=open
  Comparator #(.mode("unsigned"), .width(32)) comparator_4 (
    .a(biu_i_daddr), .b(32'h3000), .gt(comparator_4_gt), .eq(comparator_4_eq), .lt(comparator_4_lt));
  Multiplexer #(.width(32)) multiplexer_5 (
    .in0(multiplexer_4_out), .in1(biu_i_itim_rdata), .out(biu_o_drdata), .sel(is_itim_addr));
  and and_1 (is_itim_addr, or_1_out, comparator_2_lt);
  and and_2 (is_dtim_addr, or_2_out, comparator_3_lt);
  and and_3 (is_mmio_addr, or_3_out, comparator_4_lt);

  assign biu_o_dtim_wdata = biu_i_dwdata;
  assign biu_o_halt = 1'b0;
  assign biu_o_idata = biu_i_itim_rdata;
  assign biu_o_itim_addr = biu_i_iaddr;
  assign biu_o_mmio_wdata = biu_i_dwdata;

  // Other names for the same wires on the sheet: daddr[31:0] = biu_i_daddr; drdata[31:0] = biu_o_drdata;
  //   dtim_addr[31:0] = biu_o_dtim_addr; dtim_rdata[31:0] = biu_i_dtim_rdata; dtim_wmask[3:0] = biu_o_dtim_wmask;
  //   dwmask[3:0] = biu_i_dwmask; iaddr[31:0] = biu_i_iaddr; itim_addr[31:0] = biu_i_iaddr;
  //   idata[31:0] = biu_i_itim_rdata; itim_rdata[31:0] = biu_i_itim_rdata; mmio_addr[31:0] = biu_o_mmio_addr;
  //   mmio_rdata[31:0] = biu_i_mmio_rdata; dtim_wdata[31:0] = biu_i_dwdata; dwdata[31:0] = biu_i_dwdata;
  //   mmio_wdata[31:0] = biu_i_dwdata; mmio_wmask[3:0] = biu_o_mmio_wmask
endmodule
